// Logisim project ALU_Andres_y_Daniel.circ as structural Verilog: 26 circuits, main circuit main
module main (
  input  WE,
  input  [4:0] RS1,
  input  [4:0] RS2,
  input  [4:0] WS,
  input  [31:0] WD,
  output NEG,
  output OVRF
);

  wire CLK;
  wire [4:0] OP;
  wire [23:0] bit_extender_1_out;
  wire [31:0] A, B, mult_high, mult_low, OUT_ALU, PC_IN, PC_q, rom_1_data;

  Clock u_clk (.out(CLK));
  L_32_bit_register PC (.CLK(CLK), .DATA(PC_IN), .Q(PC_q));  // open: Q_neg
  ROM #(.addrWidth(24), .dataWidth(32)) rom_1 (.addr(bit_extender_1_out), .data(rom_1_data));
  Bit_Extender #(.in_width(32), .out_width(24)) bit_extender_1 (.in(PC_q), .out(bit_extender_1_out));
  L_32_bit_reg RF (
    .read_selector_1(RS1), .read_selector_2(RS2), .write_selector(WS), .write_data(WD), .hi_in(mult_high),
    .low_in(mult_low), .write_enable(WE), .clock(CLK), .output_1(A), .output_2(B));  // open: hi_out, low_out
  ALU_32_bit alu_32_bit_1 (
    .A(A), .B(B), .op(OP), .negative(NEG), .overflow(OVRF), .mult_high(mult_high), .mult_low(mult_low),
    .out1(OUT_ALU));
endmodule

module ALU_32_bit (
  input  [31:0] A,
  input  [31:0] B,
  input  [4:0] op,
  output negative,
  output overflow,
  output [31:0] mult_high,
  output [31:0] mult_low,
  output [31:0] out1
);

  wire add_overflow, addi_overflow, mult32_1_overflow;
  wire [31:0] add_result, addi_result, and1_result, beq1_out_3, bgt1_gto, blt1_lto, bne1_out_3,
       divider_1_out, j_o, jal_o, jr_o, la_o, li_o, lw_o, mfhi_o, mflo_o, move_o, or1_result, sll1_out_3,
       srl1_out_3, sub_result, sw_o;

  L_32_bit_Adder add (.A(A), .B(B), .overflow(add_overflow), .Result(add_result));
  L_32_bit_Subtractor sub (.A(A), .B(B), .negative(negative), .Result(sub_result));
  L_32_bit_Adder addi (.A(A), .B(B), .overflow(addi_overflow), .Result(addi_result));
  mult32 mult32_1 (.A(A), .B(B), .mflo(mult_low), .mfhi(mult_high), .overflow(mult32_1_overflow));
  L_32_Pass mfhi (.a(A), .b(B), .o(mfhi_o));
  L_32_Pass mflo (.a(A), .b(B), .o(mflo_o));
  L_32_bit_AND and1 (.A(A), .B(B), .Result(and1_result));
  L_32_bit_OR or1 (.A(A), .B(B), .Result(or1_result));
  sllx sll1 (.in_1(A), .in_2(B), .out_3(sll1_out_3));
  srlx srl1 (.in_1(A), .in_2(B), .out_3(srl1_out_3));
  L_32_Pass j (.a(A), .b(B), .o(j_o));
  L_32_Pass jal (.a(A), .b(B), .o(jal_o));
  L_32_Pass jr (.a(A), .b(B), .o(jr_o));
  beq beq1 (.a(A), .b(B), .out_3(beq1_out_3));
  bne bne1 (.in_1(A), .in_2(B), .out_3(bne1_out_3));
  bgt bgt1 (.a(A), .b(B), .gto(bgt1_gto));
  blt blt1 (.a(A), .b(B), .lto(blt1_lto));
  L_32_Pass move (.a(A), .b(B), .o(move_o));
  L_32_Pass li (.a(A), .b(B), .o(li_o));
  L_32_Pass la (.a(A), .b(B), .o(la_o));
  L_32_Pass lw (.a(A), .b(B), .o(lw_o));
  L_32_Pass sw (.a(A), .b(B), .o(sw_o));
  Divider #(.width(32)) divider_1 (.a(A), .b(B), .out(divider_1_out));  // open: upper, rem
  or or_1 (overflow, add_overflow, mult32_1_overflow, addi_overflow);
  Multiplexer #(.enable("false"), .select(5), .width(32)) multiplexer_1 (
    .in0(add_result), .in1(sub_result), .in2(addi_result), .in3(mult_low), .in4(divider_1_out), .in5(mfhi_o),
    .in6(mflo_o), .in7(and1_result), .in8(or1_result), .in9(sll1_out_3), .in10(srl1_out_3), .in11(j_o),
    .in12(jal_o), .in13(jr_o), .in14(beq1_out_3), .in15(bne1_out_3), .in16(bgt1_gto), .in17(blt1_lto),
    .in18(move_o), .in19(li_o), .in20(la_o), .in21(lw_o), .in22(sw_o), .out(out1), .sel(op));  // open: in23, in24, in25, in26, in27, in28, in29, in30, in31
endmodule

// +
module L_1_bit_Adder (
  input  A,
  input  B,
  input  Carry_In,
  output Carry_Out,
  output Result
);

  wire and_1_out, and_2_out, xor_1_out;

  and and_1 (and_1_out, A, B);
  xor xor_1 (xor_1_out, A, B);
  or or_1 (Carry_Out, and_1_out, and_2_out);
  and and_2 (and_2_out, Carry_In, xor_1_out);
  xor xor_2 (Result, Carry_In, xor_1_out);

  // Notes on the sheet:
  //   Full Adder
endmodule

module L_4_bit_Adder (
  input  [3:0] A,
  input  [3:0] B,
  input  Carry_In,
  output Carry_Out,
  output [3:0] Result
);

  wire l_1_bit_adder_1_carry_out, l_1_bit_adder_2_carry_out, l_1_bit_adder_3_carry_out;

  L_1_bit_Adder l_1_bit_adder_1 (
    .A(A[0]), .B(B[0]), .Carry_Out(l_1_bit_adder_1_carry_out), .Carry_In(Carry_In), .Result(Result[0]));
  L_1_bit_Adder l_1_bit_adder_2 (
    .A(A[1]), .B(B[1]), .Carry_Out(l_1_bit_adder_2_carry_out), .Carry_In(l_1_bit_adder_1_carry_out),
    .Result(Result[1]));
  L_1_bit_Adder l_1_bit_adder_3 (
    .A(A[2]), .B(B[2]), .Carry_Out(l_1_bit_adder_3_carry_out), .Carry_In(l_1_bit_adder_2_carry_out),
    .Result(Result[2]));
  L_1_bit_Adder l_1_bit_adder_4 (
    .A(A[3]), .B(B[3]), .Carry_Out(Carry_Out), .Carry_In(l_1_bit_adder_3_carry_out), .Result(Result[3]));
endmodule

module L_16_bit_Adder (
  input  [15:0] A,
  input  [15:0] B,
  input  Carry_In,
  output Carry_Out,
  output [15:0] Result
);

  wire l_4_bit_adder_1_carry_out, l_4_bit_adder_2_carry_out, l_4_bit_adder_3_carry_out;

  L_4_bit_Adder l_4_bit_adder_1 (
    .Carry_In(Carry_In), .A(A[3:0]), .B(B[3:0]), .Result(Result[3:0]), .Carry_Out(l_4_bit_adder_1_carry_out));
  L_4_bit_Adder l_4_bit_adder_2 (
    .Carry_In(l_4_bit_adder_1_carry_out), .A(A[7:4]), .B(B[7:4]), .Result(Result[7:4]),
    .Carry_Out(l_4_bit_adder_2_carry_out));
  L_4_bit_Adder l_4_bit_adder_3 (
    .Carry_In(l_4_bit_adder_2_carry_out), .A(A[11:8]), .B(B[11:8]), .Result(Result[11:8]),
    .Carry_Out(l_4_bit_adder_3_carry_out));
  L_4_bit_Adder l_4_bit_adder_4 (
    .Carry_In(l_4_bit_adder_3_carry_out), .A(A[15:12]), .B(B[15:12]), .Result(Result[15:12]),
    .Carry_Out(Carry_Out));
endmodule

module L_32_bit_AND (
  input  [31:0] A,
  input  [31:0] B,
  output [31:0] Result
);

  assign Result = A & B;  // AND_Gate and_1, 32 bits wide

  // Notes on the sheet:
  //   32-bit AND
endmodule

module L_32_bit_OR (
  input  [31:0] A,
  input  [31:0] B,
  output [31:0] Result
);

  assign Result = A | B;  // OR_Gate or_1, 32 bits wide

  // Notes on the sheet:
  //   32-bit OR
endmodule

module L_32_bit_Adder_Subtracter (
  input  [31:0] A,
  input  [31:0] B,
  input  Carry_In,
  output Carry_Out,
  output [31:0] Result
);

  wire l_16_bit_adder_1_carry_out;
  wire [15:0] bit_extender_1_out, xor_1_out, xor_2_out;

  assign bit_extender_1_out = {{15{Carry_In}}, Carry_In};  // Bit_Extender bit_extender_1
  assign xor_1_out = bit_extender_1_out ^ B[15:0];  // XOR_Gate xor_1, 16 bits wide
  L_16_bit_Adder l_16_bit_adder_1 (
    .Carry_In(Carry_In), .A(A[15:0]), .B(xor_1_out), .Result(Result[15:0]),
    .Carry_Out(l_16_bit_adder_1_carry_out));
  assign xor_2_out = bit_extender_1_out ^ B[31:16];  // XOR_Gate xor_2, 16 bits wide
  L_16_bit_Adder l_16_bit_adder_2 (
    .Carry_In(l_16_bit_adder_1_carry_out), .A(A[31:16]), .B(xor_2_out), .Result(Result[31:16]),
    .Carry_Out(Carry_Out));

  // Notes on the sheet:
  //   32 bit Adder/Subtracter
endmodule

module L_32_bit_Subtractor (
  input  [31:0] A,
  input  [31:0] B,
  output negative,
  output [31:0] Result
);

  wire l_32_bit_adder_subtracter_1_carry_out;

  not not_1 (negative, l_32_bit_adder_subtracter_1_carry_out);
  L_32_bit_Adder_Subtracter l_32_bit_adder_subtracter_1 (
    .A(A), .B(B), .Carry_Out(l_32_bit_adder_subtracter_1_carry_out), .Carry_In(1'b1), .Result(Result));
endmodule

module L_32_bit_Adder (
  input  [31:0] A,
  input  [31:0] B,
  output overflow,
  output [31:0] Result
);

  L_32_bit_Adder_Subtracter l_32_bit_adder_subtracter_1 (
    .A(A), .B(B), .Carry_Out(overflow), .Result(Result));  // open: Carry_In
endmodule

module L_32_Pass (
  input  [31:0] a,
  input  [31:0] b,
  output [31:0] o
);


  assign o = a;
endmodule

module beq (
  input  [31:0] a,
  input  [31:0] b,
  output [31:0] out_3
);

  wire and_1_out;
  wire [31:0] xnor_1_out;

  assign xnor_1_out = ~(a ^ b);  // XNOR_Gate xnor_1, 32 bits wide
  and and_1 (and_1_out, xnor_1_out[0], xnor_1_out[1], xnor_1_out[2], xnor_1_out[3], xnor_1_out[4], xnor_1_out[5], xnor_1_out[6], xnor_1_out[7], xnor_1_out[8], xnor_1_out[9], xnor_1_out[10], xnor_1_out[11], xnor_1_out[12], xnor_1_out[13], xnor_1_out[14], xnor_1_out[15], xnor_1_out[17], xnor_1_out[18], xnor_1_out[19], xnor_1_out[20], xnor_1_out[21], xnor_1_out[22], xnor_1_out[23], xnor_1_out[24], xnor_1_out[25], xnor_1_out[26], xnor_1_out[27], xnor_1_out[28], xnor_1_out[29], xnor_1_out[30], xnor_1_out[31], xnor_1_out[16]);
  assign out_3 = {{31{and_1_out}}, and_1_out};  // Bit_Extender bit_extender_1
endmodule

module bne (
  input  [31:0] in_1,
  input  [31:0] in_2,
  output [31:0] out_3
);

  wire [31:0] beq_1_out_3;

  beq beq_1 (.a(in_1), .b(in_2), .out_3(beq_1_out_3));
  assign out_3 = ~beq_1_out_3;  // NOT_Gate not_1, 32 bits wide
endmodule

module comparator_4_bit (
  input  [3:0] a,
  input  [3:0] b,
  input  gti,
  input  eqi,
  input  lti,
  output gto,
  output eqo,
  output lto
);

  wire and_3_out, and_4_out, and_5_out, and_6_out, and_7_out, nand_1_out, or_1_out, or_2_out;
  wire [3:0] and_1_out, and_2_out, not_1_out, not_2_out, xnor_1_out;

  assign not_1_out = ~a;  // NOT_Gate not_1, 4 bits wide
  assign and_1_out = a & not_2_out;  // AND_Gate and_1, 4 bits wide
  assign not_2_out = ~b;  // NOT_Gate not_2, 4 bits wide
  assign xnor_1_out = ~(b ^ a);  // XNOR_Gate xnor_1, 4 bits wide
  assign and_2_out = not_1_out & b;  // AND_Gate and_2, 4 bits wide
  or or_1 (or_1_out, and_1_out[0], and_1_out[1], and_1_out[3], and_1_out[2]);
  and and_3 (and_3_out, xnor_1_out[0], xnor_1_out[1], xnor_1_out[3], xnor_1_out[2]);
  or or_2 (or_2_out, and_2_out[0], and_2_out[1], and_2_out[3], and_2_out[2]);
  and and_4 (and_4_out, gti, and_3_out);
  and and_5 (and_5_out, and_3_out, eqi);
  and and_6 (and_6_out, and_3_out, lti);
  or or_3 (gto, or_1_out, and_4_out);
  or or_4 (lto, and_6_out, or_2_out);
  nand nand_1 (nand_1_out, gti, eqi, lti);
  and and_7 (and_7_out, nand_1_out, and_3_out);
  or or_5 (eqo, and_5_out, and_7_out);
endmodule

module bgt (
  input  [31:0] a,
  input  [31:0] b,
  output [31:0] gto
);

  wire comparator_4_bit_1_eqo, comparator_4_bit_1_gto, comparator_4_bit_1_lto, comparator_4_bit_2_eqo,
       comparator_4_bit_2_gto, comparator_4_bit_2_lto, comparator_4_bit_3_eqo, comparator_4_bit_3_gto,
       comparator_4_bit_3_lto, comparator_4_bit_4_eqo, comparator_4_bit_4_gto, comparator_4_bit_4_lto,
       comparator_4_bit_5_eqo, comparator_4_bit_5_gto, comparator_4_bit_5_lto, comparator_4_bit_6_eqo,
       comparator_4_bit_6_gto, comparator_4_bit_6_lto, comparator_4_bit_7_eqo, comparator_4_bit_7_gto,
       comparator_4_bit_7_lto, comparator_4_bit_8_eqo, comparator_4_bit_8_gto, comparator_4_bit_8_lto;

  comparator_4_bit comparator_4_bit_1 (
    .a(a[3:0]), .b(b[3:0]), .gto(comparator_4_bit_1_gto), .eqo(comparator_4_bit_1_eqo),
    .lto(comparator_4_bit_1_lto));  // open: gti, eqi, lti
  comparator_4_bit comparator_4_bit_2 (
    .a(a[7:4]), .b(b[7:4]), .gti(comparator_4_bit_1_gto), .eqi(comparator_4_bit_1_eqo),
    .lti(comparator_4_bit_1_lto), .gto(comparator_4_bit_2_gto), .eqo(comparator_4_bit_2_eqo),
    .lto(comparator_4_bit_2_lto));
  comparator_4_bit comparator_4_bit_3 (
    .a(a[11:8]), .b(b[11:8]), .gti(comparator_4_bit_2_gto), .eqi(comparator_4_bit_2_eqo),
    .lti(comparator_4_bit_2_lto), .gto(comparator_4_bit_3_gto), .eqo(comparator_4_bit_3_eqo),
    .lto(comparator_4_bit_3_lto));
  comparator_4_bit comparator_4_bit_4 (
    .a(a[15:12]), .b(b[15:12]), .gti(comparator_4_bit_3_gto), .eqi(comparator_4_bit_3_eqo),
    .lti(comparator_4_bit_3_lto), .gto(comparator_4_bit_4_gto), .eqo(comparator_4_bit_4_eqo),
    .lto(comparator_4_bit_4_lto));
  comparator_4_bit comparator_4_bit_5 (
    .a(a[19:16]), .b(b[19:16]), .gti(comparator_4_bit_4_gto), .eqi(comparator_4_bit_4_eqo),
    .lti(comparator_4_bit_4_lto), .gto(comparator_4_bit_5_gto), .eqo(comparator_4_bit_5_eqo),
    .lto(comparator_4_bit_5_lto));
  comparator_4_bit comparator_4_bit_6 (
    .a(a[23:20]), .b(b[23:20]), .gti(comparator_4_bit_5_gto), .eqi(comparator_4_bit_5_eqo),
    .lti(comparator_4_bit_5_lto), .gto(comparator_4_bit_6_gto), .eqo(comparator_4_bit_6_eqo),
    .lto(comparator_4_bit_6_lto));
  comparator_4_bit comparator_4_bit_7 (
    .a(a[27:24]), .b(b[27:24]), .gti(comparator_4_bit_6_gto), .eqi(comparator_4_bit_6_eqo),
    .lti(comparator_4_bit_6_lto), .gto(comparator_4_bit_7_gto), .eqo(comparator_4_bit_7_eqo),
    .lto(comparator_4_bit_7_lto));
  comparator_4_bit comparator_4_bit_8 (
    .a(a[31:28]), .b(b[31:28]), .gti(comparator_4_bit_7_gto), .eqi(comparator_4_bit_7_eqo),
    .lti(comparator_4_bit_7_lto), .gto(comparator_4_bit_8_gto), .eqo(comparator_4_bit_8_eqo),
    .lto(comparator_4_bit_8_lto));
  assign gto = {{31{comparator_4_bit_8_gto}}, comparator_4_bit_8_gto};  // Bit_Extender bit_extender_1
endmodule

module blt (
  input  [31:0] a,
  input  [31:0] b,
  output [31:0] lto
);

  wire comparator_4_bit_1_eqo, comparator_4_bit_1_gto, comparator_4_bit_1_lto, comparator_4_bit_2_eqo,
       comparator_4_bit_2_gto, comparator_4_bit_2_lto, comparator_4_bit_3_eqo, comparator_4_bit_3_gto,
       comparator_4_bit_3_lto, comparator_4_bit_4_eqo, comparator_4_bit_4_gto, comparator_4_bit_4_lto,
       comparator_4_bit_5_eqo, comparator_4_bit_5_gto, comparator_4_bit_5_lto, comparator_4_bit_6_eqo,
       comparator_4_bit_6_gto, comparator_4_bit_6_lto, comparator_4_bit_7_eqo, comparator_4_bit_7_gto,
       comparator_4_bit_7_lto, comparator_4_bit_8_eqo, comparator_4_bit_8_gto, comparator_4_bit_8_lto;

  comparator_4_bit comparator_4_bit_1 (
    .a(a[3:0]), .b(b[3:0]), .gto(comparator_4_bit_1_gto), .eqo(comparator_4_bit_1_eqo),
    .lto(comparator_4_bit_1_lto));  // open: gti, eqi, lti
  comparator_4_bit comparator_4_bit_2 (
    .a(a[7:4]), .b(b[7:4]), .gti(comparator_4_bit_1_gto), .eqi(comparator_4_bit_1_eqo),
    .lti(comparator_4_bit_1_lto), .gto(comparator_4_bit_2_gto), .eqo(comparator_4_bit_2_eqo),
    .lto(comparator_4_bit_2_lto));
  comparator_4_bit comparator_4_bit_3 (
    .a(a[11:8]), .b(b[11:8]), .gti(comparator_4_bit_2_gto), .eqi(comparator_4_bit_2_eqo),
    .lti(comparator_4_bit_2_lto), .gto(comparator_4_bit_3_gto), .eqo(comparator_4_bit_3_eqo),
    .lto(comparator_4_bit_3_lto));
  comparator_4_bit comparator_4_bit_4 (
    .a(a[15:12]), .b(b[15:12]), .gti(comparator_4_bit_3_gto), .eqi(comparator_4_bit_3_eqo),
    .lti(comparator_4_bit_3_lto), .gto(comparator_4_bit_4_gto), .eqo(comparator_4_bit_4_eqo),
    .lto(comparator_4_bit_4_lto));
  comparator_4_bit comparator_4_bit_5 (
    .a(a[19:16]), .b(b[19:16]), .gti(comparator_4_bit_4_gto), .eqi(comparator_4_bit_4_eqo),
    .lti(comparator_4_bit_4_lto), .gto(comparator_4_bit_5_gto), .eqo(comparator_4_bit_5_eqo),
    .lto(comparator_4_bit_5_lto));
  comparator_4_bit comparator_4_bit_6 (
    .a(a[23:20]), .b(b[23:20]), .gti(comparator_4_bit_5_gto), .eqi(comparator_4_bit_5_eqo),
    .lti(comparator_4_bit_5_lto), .gto(comparator_4_bit_6_gto), .eqo(comparator_4_bit_6_eqo),
    .lto(comparator_4_bit_6_lto));
  comparator_4_bit comparator_4_bit_7 (
    .a(a[27:24]), .b(b[27:24]), .gti(comparator_4_bit_6_gto), .eqi(comparator_4_bit_6_eqo),
    .lti(comparator_4_bit_6_lto), .gto(comparator_4_bit_7_gto), .eqo(comparator_4_bit_7_eqo),
    .lto(comparator_4_bit_7_lto));
  comparator_4_bit comparator_4_bit_8 (
    .a(a[31:28]), .b(b[31:28]), .gti(comparator_4_bit_7_gto), .eqi(comparator_4_bit_7_eqo),
    .lti(comparator_4_bit_7_lto), .gto(comparator_4_bit_8_gto), .eqo(comparator_4_bit_8_eqo),
    .lto(comparator_4_bit_8_lto));
  assign lto = {{31{comparator_4_bit_8_lto}}, comparator_4_bit_8_lto};  // Bit_Extender bit_extender_1
endmodule

module L_32_bit_SRL (
  input  [31:0] B,
  input  [31:0] A,
  output [31:0] out_3
);

  wire multiplexer_1_out, multiplexer_2_out, multiplexer_3_out, multiplexer_4_out, multiplexer_5_out,
       multiplexer_6_out, multiplexer_7_out, multiplexer_8_out, multiplexer_9_out, multiplexer_10_out,
       multiplexer_11_out, multiplexer_12_out, multiplexer_13_out, multiplexer_14_out, multiplexer_15_out,
       multiplexer_16_out, multiplexer_17_out, multiplexer_18_out, multiplexer_19_out, multiplexer_20_out,
       multiplexer_21_out, multiplexer_22_out, multiplexer_23_out, multiplexer_24_out, multiplexer_25_out,
       multiplexer_26_out, multiplexer_27_out, multiplexer_28_out, multiplexer_29_out, multiplexer_30_out,
       multiplexer_31_out, multiplexer_32_out, multiplexer_33_out, multiplexer_34_out, multiplexer_35_out,
       multiplexer_36_out, multiplexer_37_out, multiplexer_38_out, multiplexer_39_out, multiplexer_40_out,
       multiplexer_41_out, multiplexer_42_out, multiplexer_43_out, multiplexer_44_out, multiplexer_45_out,
       multiplexer_46_out, multiplexer_47_out, multiplexer_48_out, multiplexer_49_out, multiplexer_50_out,
       multiplexer_51_out, multiplexer_52_out, multiplexer_53_out, multiplexer_54_out, multiplexer_55_out,
       multiplexer_56_out, multiplexer_57_out, multiplexer_58_out, multiplexer_59_out, multiplexer_60_out,
       multiplexer_61_out, multiplexer_62_out, multiplexer_63_out, multiplexer_64_out, multiplexer_65_out,
       multiplexer_66_out, multiplexer_67_out, multiplexer_68_out, multiplexer_69_out, multiplexer_70_out,
       multiplexer_71_out, multiplexer_72_out, multiplexer_73_out, multiplexer_74_out, multiplexer_75_out,
       multiplexer_76_out, multiplexer_77_out, multiplexer_78_out, multiplexer_79_out, multiplexer_80_out,
       multiplexer_81_out, multiplexer_82_out, multiplexer_83_out, multiplexer_84_out, multiplexer_85_out,
       multiplexer_86_out, multiplexer_87_out, multiplexer_88_out, multiplexer_89_out, multiplexer_90_out,
       multiplexer_91_out, multiplexer_92_out, multiplexer_93_out, multiplexer_94_out, multiplexer_95_out,
       multiplexer_96_out, multiplexer_97_out, multiplexer_98_out, multiplexer_99_out, multiplexer_100_out,
       multiplexer_101_out, multiplexer_102_out, multiplexer_103_out, multiplexer_104_out,
       multiplexer_105_out, multiplexer_106_out, multiplexer_107_out, multiplexer_108_out,
       multiplexer_109_out, multiplexer_110_out, multiplexer_111_out, multiplexer_112_out,
       multiplexer_113_out, multiplexer_114_out, multiplexer_115_out, multiplexer_116_out,
       multiplexer_117_out, multiplexer_118_out, multiplexer_119_out, multiplexer_120_out,
       multiplexer_121_out, multiplexer_122_out, multiplexer_123_out, multiplexer_124_out,
       multiplexer_125_out, multiplexer_126_out, multiplexer_127_out, multiplexer_128_out;
  wire [4:0] bit_extender_1_out;

  Bit_Extender #(.in_width(32), .out_width(5)) bit_extender_1 (.in(B), .out(bit_extender_1_out));
  Multiplexer #(.enable("false")) multiplexer_1 (
    .in0(A[31]), .in1(1'b0), .out(multiplexer_1_out), .sel(bit_extender_1_out[0]));
  Multiplexer #(.enable("false")) multiplexer_2 (
    .in0(A[30]), .in1(A[31]), .out(multiplexer_2_out), .sel(bit_extender_1_out[0]));
  Multiplexer #(.enable("false")) multiplexer_3 (
    .in0(A[29]), .in1(A[30]), .out(multiplexer_3_out), .sel(bit_extender_1_out[0]));
  Multiplexer #(.enable("false")) multiplexer_4 (
    .in0(A[28]), .in1(A[29]), .out(multiplexer_4_out), .sel(bit_extender_1_out[0]));
  Multiplexer #(.enable("false")) multiplexer_5 (
    .in0(A[27]), .in1(A[28]), .out(multiplexer_5_out), .sel(bit_extender_1_out[0]));
  Multiplexer #(.enable("false")) multiplexer_6 (
    .in0(A[26]), .in1(A[27]), .out(multiplexer_6_out), .sel(bit_extender_1_out[0]));
  Multiplexer #(.enable("false")) multiplexer_7 (
    .in0(A[25]), .in1(A[26]), .out(multiplexer_7_out), .sel(bit_extender_1_out[0]));
  Multiplexer #(.enable("false")) multiplexer_8 (
    .in0(A[24]), .in1(A[25]), .out(multiplexer_8_out), .sel(bit_extender_1_out[0]));
  Multiplexer #(.enable("false")) multiplexer_9 (
    .in0(A[23]), .in1(A[24]), .out(multiplexer_9_out), .sel(bit_extender_1_out[0]));
  Multiplexer #(.enable("false")) multiplexer_10 (
    .in0(A[22]), .in1(A[23]), .out(multiplexer_10_out), .sel(bit_extender_1_out[0]));
  Multiplexer #(.enable("false")) multiplexer_11 (
    .in0(A[21]), .in1(A[22]), .out(multiplexer_11_out), .sel(bit_extender_1_out[0]));
  Multiplexer #(.enable("false")) multiplexer_12 (
    .in0(A[20]), .in1(A[21]), .out(multiplexer_12_out), .sel(bit_extender_1_out[0]));
  Multiplexer #(.enable("false")) multiplexer_13 (
    .in0(A[19]), .in1(A[20]), .out(multiplexer_13_out), .sel(bit_extender_1_out[0]));
  Multiplexer #(.enable("false")) multiplexer_14 (
    .in0(A[18]), .in1(A[19]), .out(multiplexer_14_out), .sel(bit_extender_1_out[0]));
  Multiplexer #(.enable("false")) multiplexer_15 (
    .in0(A[17]), .in1(A[18]), .out(multiplexer_15_out), .sel(bit_extender_1_out[0]));
  Multiplexer #(.enable("false")) multiplexer_16 (
    .in0(A[16]), .in1(A[17]), .out(multiplexer_16_out), .sel(bit_extender_1_out[0]));
  Multiplexer #(.enable("false")) multiplexer_17 (
    .in0(A[15]), .in1(A[16]), .out(multiplexer_17_out), .sel(bit_extender_1_out[0]));
  Multiplexer #(.enable("false")) multiplexer_18 (
    .in0(A[14]), .in1(A[15]), .out(multiplexer_18_out), .sel(bit_extender_1_out[0]));
  Multiplexer #(.enable("false")) multiplexer_19 (
    .in0(A[13]), .in1(A[14]), .out(multiplexer_19_out), .sel(bit_extender_1_out[0]));
  Multiplexer #(.enable("false")) multiplexer_20 (
    .in0(A[12]), .in1(A[13]), .out(multiplexer_20_out), .sel(bit_extender_1_out[0]));
  Multiplexer #(.enable("false")) multiplexer_21 (
    .in0(A[11]), .in1(A[12]), .out(multiplexer_21_out), .sel(bit_extender_1_out[0]));
  Multiplexer #(.enable("false")) multiplexer_22 (
    .in0(A[10]), .in1(A[11]), .out(multiplexer_22_out), .sel(bit_extender_1_out[0]));
  Multiplexer #(.enable("false")) multiplexer_23 (
    .in0(A[9]), .in1(A[10]), .out(multiplexer_23_out), .sel(bit_extender_1_out[0]));
  Multiplexer #(.enable("false")) multiplexer_24 (
    .in0(A[8]), .in1(A[9]), .out(multiplexer_24_out), .sel(bit_extender_1_out[0]));
  Multiplexer #(.enable("false")) multiplexer_25 (
    .in0(A[7]), .in1(A[8]), .out(multiplexer_25_out), .sel(bit_extender_1_out[0]));
  Multiplexer #(.enable("false")) multiplexer_26 (
    .in0(A[6]), .in1(A[7]), .out(multiplexer_26_out), .sel(bit_extender_1_out[0]));
  Multiplexer #(.enable("false")) multiplexer_27 (
    .in0(A[5]), .in1(A[6]), .out(multiplexer_27_out), .sel(bit_extender_1_out[0]));
  Multiplexer #(.enable("false")) multiplexer_28 (
    .in0(A[4]), .in1(A[5]), .out(multiplexer_28_out), .sel(bit_extender_1_out[0]));
  Multiplexer #(.enable("false")) multiplexer_29 (
    .in0(A[3]), .in1(A[4]), .out(multiplexer_29_out), .sel(bit_extender_1_out[0]));
  Multiplexer #(.enable("false")) multiplexer_30 (
    .in0(A[2]), .in1(A[3]), .out(multiplexer_30_out), .sel(bit_extender_1_out[0]));
  Multiplexer #(.enable("false")) multiplexer_31 (
    .in0(A[1]), .in1(A[2]), .out(multiplexer_31_out), .sel(bit_extender_1_out[0]));
  Multiplexer #(.enable("false")) multiplexer_32 (
    .in0(A[0]), .in1(A[1]), .out(multiplexer_32_out), .sel(bit_extender_1_out[0]));
  Multiplexer #(.enable("false")) multiplexer_33 (
    .in0(multiplexer_1_out), .in1(1'b0), .out(multiplexer_33_out), .sel(bit_extender_1_out[1]));
  Multiplexer #(.enable("false")) multiplexer_34 (
    .in0(multiplexer_2_out), .in1(1'b0), .out(multiplexer_34_out), .sel(bit_extender_1_out[1]));
  Multiplexer #(.enable("false")) multiplexer_35 (
    .in0(multiplexer_3_out), .in1(multiplexer_1_out), .out(multiplexer_35_out), .sel(bit_extender_1_out[1]));
  Multiplexer #(.enable("false")) multiplexer_36 (
    .in0(multiplexer_4_out), .in1(multiplexer_2_out), .out(multiplexer_36_out), .sel(bit_extender_1_out[1]));
  Multiplexer #(.enable("false")) multiplexer_37 (
    .in0(multiplexer_5_out), .in1(multiplexer_3_out), .out(multiplexer_37_out), .sel(bit_extender_1_out[1]));
  Multiplexer #(.enable("false")) multiplexer_38 (
    .in0(multiplexer_6_out), .in1(multiplexer_4_out), .out(multiplexer_38_out), .sel(bit_extender_1_out[1]));
  Multiplexer #(.enable("false")) multiplexer_39 (
    .in0(multiplexer_7_out), .in1(multiplexer_5_out), .out(multiplexer_39_out), .sel(bit_extender_1_out[1]));
  Multiplexer #(.enable("false")) multiplexer_40 (
    .in0(multiplexer_8_out), .in1(multiplexer_6_out), .out(multiplexer_40_out), .sel(bit_extender_1_out[1]));
  Multiplexer #(.enable("false")) multiplexer_41 (
    .in0(multiplexer_9_out), .in1(multiplexer_7_out), .out(multiplexer_41_out), .sel(bit_extender_1_out[1]));
  Multiplexer #(.enable("false")) multiplexer_42 (
    .in0(multiplexer_10_out), .in1(multiplexer_8_out), .out(multiplexer_42_out), .sel(bit_extender_1_out[1]));
  Multiplexer #(.enable("false")) multiplexer_43 (
    .in0(multiplexer_11_out), .in1(multiplexer_9_out), .out(multiplexer_43_out), .sel(bit_extender_1_out[1]));
  Multiplexer #(.enable("false")) multiplexer_44 (
    .in0(multiplexer_12_out), .in1(multiplexer_10_out), .out(multiplexer_44_out), .sel(bit_extender_1_out[1]));
  Multiplexer #(.enable("false")) multiplexer_45 (
    .in0(multiplexer_13_out), .in1(multiplexer_11_out), .out(multiplexer_45_out), .sel(bit_extender_1_out[1]));
  Multiplexer #(.enable("false")) multiplexer_46 (
    .in0(multiplexer_14_out), .in1(multiplexer_12_out), .out(multiplexer_46_out), .sel(bit_extender_1_out[1]));
  Multiplexer #(.enable("false")) multiplexer_47 (
    .in0(multiplexer_15_out), .in1(multiplexer_13_out), .out(multiplexer_47_out), .sel(bit_extender_1_out[1]));
  Multiplexer #(.enable("false")) multiplexer_48 (
    .in0(multiplexer_16_out), .in1(multiplexer_14_out), .out(multiplexer_48_out), .sel(bit_extender_1_out[1]));
  Multiplexer #(.enable("false")) multiplexer_49 (
    .in0(multiplexer_17_out), .in1(multiplexer_15_out), .out(multiplexer_49_out), .sel(bit_extender_1_out[1]));
  Multiplexer #(.enable("false")) multiplexer_50 (
    .in0(multiplexer_18_out), .in1(multiplexer_16_out), .out(multiplexer_50_out), .sel(bit_extender_1_out[1]));
  Multiplexer #(.enable("false")) multiplexer_51 (
    .in0(multiplexer_19_out), .in1(multiplexer_17_out), .out(multiplexer_51_out), .sel(bit_extender_1_out[1]));
  Multiplexer #(.enable("false")) multiplexer_52 (
    .in0(multiplexer_20_out), .in1(multiplexer_18_out), .out(multiplexer_52_out), .sel(bit_extender_1_out[1]));
  Multiplexer #(.enable("false")) multiplexer_53 (
    .in0(multiplexer_21_out), .in1(multiplexer_19_out), .out(multiplexer_53_out), .sel(bit_extender_1_out[1]));
  Multiplexer #(.enable("false")) multiplexer_54 (
    .in0(multiplexer_22_out), .in1(multiplexer_20_out), .out(multiplexer_54_out), .sel(bit_extender_1_out[1]));
  Multiplexer #(.enable("false")) multiplexer_55 (
    .in0(multiplexer_23_out), .in1(multiplexer_21_out), .out(multiplexer_55_out), .sel(bit_extender_1_out[1]));
  Multiplexer #(.enable("false")) multiplexer_56 (
    .in0(multiplexer_24_out), .in1(multiplexer_22_out), .out(multiplexer_56_out), .sel(bit_extender_1_out[1]));
  Multiplexer #(.enable("false")) multiplexer_57 (
    .in0(multiplexer_25_out), .in1(multiplexer_23_out), .out(multiplexer_57_out), .sel(bit_extender_1_out[1]));
  Multiplexer #(.enable("false")) multiplexer_58 (
    .in0(multiplexer_26_out), .in1(multiplexer_24_out), .out(multiplexer_58_out), .sel(bit_extender_1_out[1]));
  Multiplexer #(.enable("false")) multiplexer_59 (
    .in0(multiplexer_27_out), .in1(multiplexer_25_out), .out(multiplexer_59_out), .sel(bit_extender_1_out[1]));
  Multiplexer #(.enable("false")) multiplexer_60 (
    .in0(multiplexer_28_out), .in1(multiplexer_26_out), .out(multiplexer_60_out), .sel(bit_extender_1_out[1]));
  Multiplexer #(.enable("false")) multiplexer_61 (
    .in0(multiplexer_29_out), .in1(multiplexer_27_out), .out(multiplexer_61_out), .sel(bit_extender_1_out[1]));
  Multiplexer #(.enable("false")) multiplexer_62 (
    .in0(multiplexer_30_out), .in1(multiplexer_28_out), .out(multiplexer_62_out), .sel(bit_extender_1_out[1]));
  Multiplexer #(.enable("false")) multiplexer_63 (
    .in0(multiplexer_31_out), .in1(multiplexer_29_out), .out(multiplexer_63_out), .sel(bit_extender_1_out[1]));
  Multiplexer #(.enable("false")) multiplexer_64 (
    .in0(multiplexer_32_out), .in1(multiplexer_30_out), .out(multiplexer_64_out), .sel(bit_extender_1_out[1]));
  Multiplexer #(.enable("false")) multiplexer_65 (
    .in0(multiplexer_33_out), .in1(1'b0), .out(multiplexer_65_out), .sel(bit_extender_1_out[2]));
  Multiplexer #(.enable("false")) multiplexer_66 (
    .in0(multiplexer_34_out), .in1(1'b0), .out(multiplexer_66_out), .sel(bit_extender_1_out[2]));
  Multiplexer #(.enable("false")) multiplexer_67 (
    .in0(multiplexer_35_out), .in1(1'b0), .out(multiplexer_67_out), .sel(bit_extender_1_out[2]));
  Multiplexer #(.enable("false")) multiplexer_68 (
    .in0(multiplexer_36_out), .in1(1'b0), .out(multiplexer_68_out), .sel(bit_extender_1_out[2]));
  Multiplexer #(.enable("false")) multiplexer_69 (
    .in0(multiplexer_37_out), .in1(multiplexer_33_out), .out(multiplexer_69_out), .sel(bit_extender_1_out[2]));
  Multiplexer #(.enable("false")) multiplexer_70 (
    .in0(multiplexer_38_out), .in1(multiplexer_34_out), .out(multiplexer_70_out), .sel(bit_extender_1_out[2]));
  Multiplexer #(.enable("false")) multiplexer_71 (
    .in0(multiplexer_39_out), .in1(multiplexer_35_out), .out(multiplexer_71_out), .sel(bit_extender_1_out[2]));
  Multiplexer #(.enable("false")) multiplexer_72 (
    .in0(multiplexer_40_out), .in1(multiplexer_36_out), .out(multiplexer_72_out), .sel(bit_extender_1_out[2]));
  Multiplexer #(.enable("false")) multiplexer_73 (
    .in0(multiplexer_41_out), .in1(multiplexer_37_out), .out(multiplexer_73_out), .sel(bit_extender_1_out[2]));
  Multiplexer #(.enable("false")) multiplexer_74 (
    .in0(multiplexer_42_out), .in1(multiplexer_38_out), .out(multiplexer_74_out), .sel(bit_extender_1_out[2]));
  Multiplexer #(.enable("false")) multiplexer_75 (
    .in0(multiplexer_43_out), .in1(multiplexer_39_out), .out(multiplexer_75_out), .sel(bit_extender_1_out[2]));
  Multiplexer #(.enable("false")) multiplexer_76 (
    .in0(multiplexer_44_out), .in1(multiplexer_40_out), .out(multiplexer_76_out), .sel(bit_extender_1_out[2]));
  Multiplexer #(.enable("false")) multiplexer_77 (
    .in0(multiplexer_45_out), .in1(multiplexer_41_out), .out(multiplexer_77_out), .sel(bit_extender_1_out[2]));
  Multiplexer #(.enable("false")) multiplexer_78 (
    .in0(multiplexer_46_out), .in1(multiplexer_42_out), .out(multiplexer_78_out), .sel(bit_extender_1_out[2]));
  Multiplexer #(.enable("false")) multiplexer_79 (
    .in0(multiplexer_47_out), .in1(multiplexer_43_out), .out(multiplexer_79_out), .sel(bit_extender_1_out[2]));
  Multiplexer #(.enable("false")) multiplexer_80 (
    .in0(multiplexer_48_out), .in1(multiplexer_44_out), .out(multiplexer_80_out), .sel(bit_extender_1_out[2]));
  Multiplexer #(.enable("false")) multiplexer_81 (
    .in0(multiplexer_49_out), .in1(multiplexer_45_out), .out(multiplexer_81_out), .sel(bit_extender_1_out[2]));
  Multiplexer #(.enable("false")) multiplexer_82 (
    .in0(multiplexer_50_out), .in1(multiplexer_46_out), .out(multiplexer_82_out), .sel(bit_extender_1_out[2]));
  Multiplexer #(.enable("false")) multiplexer_83 (
    .in0(multiplexer_51_out), .in1(multiplexer_47_out), .out(multiplexer_83_out), .sel(bit_extender_1_out[2]));
  Multiplexer #(.enable("false")) multiplexer_84 (
    .in0(multiplexer_52_out), .in1(multiplexer_48_out), .out(multiplexer_84_out), .sel(bit_extender_1_out[2]));
  Multiplexer #(.enable("false")) multiplexer_85 (
    .in0(multiplexer_53_out), .in1(multiplexer_49_out), .out(multiplexer_85_out), .sel(bit_extender_1_out[2]));
  Multiplexer #(.enable("false")) multiplexer_86 (
    .in0(multiplexer_54_out), .in1(multiplexer_50_out), .out(multiplexer_86_out), .sel(bit_extender_1_out[2]));
  Multiplexer #(.enable("false")) multiplexer_87 (
    .in0(multiplexer_55_out), .in1(multiplexer_51_out), .out(multiplexer_87_out), .sel(bit_extender_1_out[2]));
  Multiplexer #(.enable("false")) multiplexer_88 (
    .in0(multiplexer_56_out), .in1(multiplexer_52_out), .out(multiplexer_88_out), .sel(bit_extender_1_out[2]));
  Multiplexer #(.enable("false")) multiplexer_89 (
    .in0(multiplexer_57_out), .in1(multiplexer_53_out), .out(multiplexer_89_out), .sel(bit_extender_1_out[2]));
  Multiplexer #(.enable("false")) multiplexer_90 (
    .in0(multiplexer_58_out), .in1(multiplexer_54_out), .out(multiplexer_90_out), .sel(bit_extender_1_out[2]));
  Multiplexer #(.enable("false")) multiplexer_91 (
    .in0(multiplexer_59_out), .in1(multiplexer_55_out), .out(multiplexer_91_out), .sel(bit_extender_1_out[2]));
  Multiplexer #(.enable("false")) multiplexer_92 (
    .in0(multiplexer_60_out), .in1(multiplexer_56_out), .out(multiplexer_92_out), .sel(bit_extender_1_out[2]));
  Multiplexer #(.enable("false")) multiplexer_93 (
    .in0(multiplexer_61_out), .in1(multiplexer_57_out), .out(multiplexer_93_out), .sel(bit_extender_1_out[2]));
  Multiplexer #(.enable("false")) multiplexer_94 (
    .in0(multiplexer_62_out), .in1(multiplexer_58_out), .out(multiplexer_94_out), .sel(bit_extender_1_out[2]));
  Multiplexer #(.enable("false")) multiplexer_95 (
    .in0(multiplexer_63_out), .in1(multiplexer_59_out), .out(multiplexer_95_out), .sel(bit_extender_1_out[2]));
  Multiplexer #(.enable("false")) multiplexer_96 (
    .in0(multiplexer_64_out), .in1(multiplexer_60_out), .out(multiplexer_96_out), .sel(bit_extender_1_out[2]));
  Multiplexer #(.enable("false")) multiplexer_97 (
    .in0(multiplexer_65_out), .in1(1'b0), .out(multiplexer_97_out), .sel(bit_extender_1_out[3]));
  Multiplexer #(.enable("false")) multiplexer_98 (
    .in0(multiplexer_66_out), .in1(1'b0), .out(multiplexer_98_out), .sel(bit_extender_1_out[3]));
  Multiplexer #(.enable("false")) multiplexer_99 (
    .in0(multiplexer_67_out), .in1(1'b0), .out(multiplexer_99_out), .sel(bit_extender_1_out[3]));
  Multiplexer #(.enable("false")) multiplexer_100 (
    .in0(multiplexer_68_out), .in1(1'b0), .out(multiplexer_100_out), .sel(bit_extender_1_out[3]));
  Multiplexer #(.enable("false")) multiplexer_101 (
    .in0(multiplexer_69_out), .in1(1'b0), .out(multiplexer_101_out), .sel(bit_extender_1_out[3]));
  Multiplexer #(.enable("false")) multiplexer_102 (
    .in0(multiplexer_70_out), .in1(1'b0), .out(multiplexer_102_out), .sel(bit_extender_1_out[3]));
  Multiplexer #(.enable("false")) multiplexer_103 (
    .in0(multiplexer_71_out), .in1(1'b0), .out(multiplexer_103_out), .sel(bit_extender_1_out[3]));
  Multiplexer #(.enable("false")) multiplexer_104 (
    .in0(multiplexer_72_out), .in1(1'b0), .out(multiplexer_104_out), .sel(bit_extender_1_out[3]));
  Multiplexer #(.enable("false")) multiplexer_105 (
    .in0(multiplexer_73_out), .in1(multiplexer_65_out), .out(multiplexer_105_out), .sel(bit_extender_1_out[3]));
  Multiplexer #(.enable("false")) multiplexer_106 (
    .in0(multiplexer_74_out), .in1(multiplexer_66_out), .out(multiplexer_106_out), .sel(bit_extender_1_out[3]));
  Multiplexer #(.enable("false")) multiplexer_107 (
    .in0(multiplexer_75_out), .in1(multiplexer_67_out), .out(multiplexer_107_out), .sel(bit_extender_1_out[3]));
  Multiplexer #(.enable("false")) multiplexer_108 (
    .in0(multiplexer_76_out), .in1(multiplexer_68_out), .out(multiplexer_108_out), .sel(bit_extender_1_out[3]));
  Multiplexer #(.enable("false")) multiplexer_109 (
    .in0(multiplexer_77_out), .in1(multiplexer_69_out), .out(multiplexer_109_out), .sel(bit_extender_1_out[3]));
  Multiplexer #(.enable("false")) multiplexer_110 (
    .in0(multiplexer_78_out), .in1(multiplexer_70_out), .out(multiplexer_110_out), .sel(bit_extender_1_out[3]));
  Multiplexer #(.enable("false")) multiplexer_111 (
    .in0(multiplexer_79_out), .in1(multiplexer_71_out), .out(multiplexer_111_out), .sel(bit_extender_1_out[3]));
  Multiplexer #(.enable("false")) multiplexer_112 (
    .in0(multiplexer_80_out), .in1(multiplexer_72_out), .out(multiplexer_112_out), .sel(bit_extender_1_out[3]));
  Multiplexer #(.enable("false")) multiplexer_113 (
    .in0(multiplexer_81_out), .in1(multiplexer_73_out), .out(multiplexer_113_out), .sel(bit_extender_1_out[3]));
  Multiplexer #(.enable("false")) multiplexer_114 (
    .in0(multiplexer_82_out), .in1(multiplexer_74_out), .out(multiplexer_114_out), .sel(bit_extender_1_out[3]));
  Multiplexer #(.enable("false")) multiplexer_115 (
    .in0(multiplexer_83_out), .in1(multiplexer_75_out), .out(multiplexer_115_out), .sel(bit_extender_1_out[3]));
  Multiplexer #(.enable("false")) multiplexer_116 (
    .in0(multiplexer_84_out), .in1(multiplexer_76_out), .out(multiplexer_116_out), .sel(bit_extender_1_out[3]));
  Multiplexer #(.enable("false")) multiplexer_117 (
    .in0(multiplexer_85_out), .in1(multiplexer_77_out), .out(multiplexer_117_out), .sel(bit_extender_1_out[3]));
  Multiplexer #(.enable("false")) multiplexer_118 (
    .in0(multiplexer_86_out), .in1(multiplexer_78_out), .out(multiplexer_118_out), .sel(bit_extender_1_out[3]));
  Multiplexer #(.enable("false")) multiplexer_119 (
    .in0(multiplexer_87_out), .in1(multiplexer_79_out), .out(multiplexer_119_out), .sel(bit_extender_1_out[3]));
  Multiplexer #(.enable("false")) multiplexer_120 (
    .in0(multiplexer_88_out), .in1(multiplexer_80_out), .out(multiplexer_120_out), .sel(bit_extender_1_out[3]));
  Multiplexer #(.enable("false")) multiplexer_121 (
    .in0(multiplexer_89_out), .in1(multiplexer_81_out), .out(multiplexer_121_out), .sel(bit_extender_1_out[3]));
  Multiplexer #(.enable("false")) multiplexer_122 (
    .in0(multiplexer_90_out), .in1(multiplexer_82_out), .out(multiplexer_122_out), .sel(bit_extender_1_out[3]));
  Multiplexer #(.enable("false")) multiplexer_123 (
    .in0(multiplexer_91_out), .in1(multiplexer_83_out), .out(multiplexer_123_out), .sel(bit_extender_1_out[3]));
  Multiplexer #(.enable("false")) multiplexer_124 (
    .in0(multiplexer_92_out), .in1(multiplexer_84_out), .out(multiplexer_124_out), .sel(bit_extender_1_out[3]));
  Multiplexer #(.enable("false")) multiplexer_125 (
    .in0(multiplexer_93_out), .in1(multiplexer_85_out), .out(multiplexer_125_out), .sel(bit_extender_1_out[3]));
  Multiplexer #(.enable("false")) multiplexer_126 (
    .in0(multiplexer_94_out), .in1(multiplexer_86_out), .out(multiplexer_126_out), .sel(bit_extender_1_out[3]));
  Multiplexer #(.enable("false")) multiplexer_127 (
    .in0(multiplexer_95_out), .in1(multiplexer_87_out), .out(multiplexer_127_out), .sel(bit_extender_1_out[3]));
  Multiplexer #(.enable("false")) multiplexer_128 (
    .in0(multiplexer_96_out), .in1(multiplexer_88_out), .out(multiplexer_128_out), .sel(bit_extender_1_out[3]));
  Multiplexer #(.enable("false")) multiplexer_129 (
    .in0(multiplexer_97_out), .in1(1'b0), .out(out_3[31]), .sel(bit_extender_1_out[4]));
  Multiplexer #(.enable("false")) multiplexer_130 (
    .in0(multiplexer_98_out), .in1(1'b0), .out(out_3[30]), .sel(bit_extender_1_out[4]));
  Multiplexer #(.enable("false")) multiplexer_131 (
    .in0(multiplexer_99_out), .in1(1'b0), .out(out_3[29]), .sel(bit_extender_1_out[4]));
  Multiplexer #(.enable("false")) multiplexer_132 (
    .in0(multiplexer_100_out), .in1(1'b0), .out(out_3[28]), .sel(bit_extender_1_out[4]));
  Multiplexer #(.enable("false")) multiplexer_133 (
    .in0(multiplexer_101_out), .in1(1'b0), .out(out_3[27]), .sel(bit_extender_1_out[4]));
  Multiplexer #(.enable("false")) multiplexer_134 (
    .in0(multiplexer_102_out), .in1(1'b0), .out(out_3[26]), .sel(bit_extender_1_out[4]));
  Multiplexer #(.enable("false")) multiplexer_135 (
    .in0(multiplexer_103_out), .in1(1'b0), .out(out_3[25]), .sel(bit_extender_1_out[4]));
  Multiplexer #(.enable("false")) multiplexer_136 (
    .in0(multiplexer_104_out), .in1(1'b0), .out(out_3[24]), .sel(bit_extender_1_out[4]));
  Multiplexer #(.enable("false")) multiplexer_137 (
    .in0(multiplexer_105_out), .in1(1'b0), .out(out_3[23]), .sel(bit_extender_1_out[4]));
  Multiplexer #(.enable("false")) multiplexer_138 (
    .in0(multiplexer_106_out), .in1(1'b0), .out(out_3[22]), .sel(bit_extender_1_out[4]));
  Multiplexer #(.enable("false")) multiplexer_139 (
    .in0(multiplexer_107_out), .in1(1'b0), .out(out_3[21]), .sel(bit_extender_1_out[4]));
  Multiplexer #(.enable("false")) multiplexer_140 (
    .in0(multiplexer_108_out), .in1(1'b0), .out(out_3[20]), .sel(bit_extender_1_out[4]));
  Multiplexer #(.enable("false")) multiplexer_141 (
    .in0(multiplexer_109_out), .in1(1'b0), .out(out_3[19]), .sel(bit_extender_1_out[4]));
  Multiplexer #(.enable("false")) multiplexer_142 (
    .in0(multiplexer_110_out), .in1(1'b0), .out(out_3[18]), .sel(bit_extender_1_out[4]));
  Multiplexer #(.enable("false")) multiplexer_143 (
    .in0(multiplexer_111_out), .in1(1'b0), .out(out_3[17]), .sel(bit_extender_1_out[4]));
  Multiplexer #(.enable("false")) multiplexer_144 (
    .in0(multiplexer_112_out), .in1(1'b0), .out(out_3[16]), .sel(bit_extender_1_out[4]));
  Multiplexer #(.enable("false")) multiplexer_145 (
    .in0(multiplexer_113_out), .in1(multiplexer_97_out), .out(out_3[15]), .sel(bit_extender_1_out[4]));
  Multiplexer #(.enable("false")) multiplexer_146 (
    .in0(multiplexer_114_out), .in1(multiplexer_98_out), .out(out_3[14]), .sel(bit_extender_1_out[4]));
  Multiplexer #(.enable("false")) multiplexer_147 (
    .in0(multiplexer_115_out), .in1(multiplexer_99_out), .out(out_3[13]), .sel(bit_extender_1_out[4]));
  Multiplexer #(.enable("false")) multiplexer_148 (
    .in0(multiplexer_116_out), .in1(multiplexer_100_out), .out(out_3[12]), .sel(bit_extender_1_out[4]));
  Multiplexer #(.enable("false")) multiplexer_149 (
    .in0(multiplexer_117_out), .in1(multiplexer_101_out), .out(out_3[11]), .sel(bit_extender_1_out[4]));
  Multiplexer #(.enable("false")) multiplexer_150 (
    .in0(multiplexer_118_out), .in1(multiplexer_102_out), .out(out_3[10]), .sel(bit_extender_1_out[4]));
  Multiplexer #(.enable("false")) multiplexer_151 (
    .in0(multiplexer_119_out), .in1(multiplexer_103_out), .out(out_3[9]), .sel(bit_extender_1_out[4]));
  Multiplexer #(.enable("false")) multiplexer_152 (
    .in0(multiplexer_120_out), .in1(multiplexer_104_out), .out(out_3[8]), .sel(bit_extender_1_out[4]));
  Multiplexer #(.enable("false")) multiplexer_153 (
    .in0(multiplexer_121_out), .in1(multiplexer_105_out), .out(out_3[7]), .sel(bit_extender_1_out[4]));
  Multiplexer #(.enable("false")) multiplexer_154 (
    .in0(multiplexer_122_out), .in1(multiplexer_106_out), .out(out_3[6]), .sel(bit_extender_1_out[4]));
  Multiplexer #(.enable("false")) multiplexer_155 (
    .in0(multiplexer_123_out), .in1(multiplexer_107_out), .out(out_3[5]), .sel(bit_extender_1_out[4]));
  Multiplexer #(.enable("false")) multiplexer_156 (
    .in0(multiplexer_124_out), .in1(multiplexer_108_out), .out(out_3[4]), .sel(bit_extender_1_out[4]));
  Multiplexer #(.enable("false")) multiplexer_157 (
    .in0(multiplexer_125_out), .in1(multiplexer_109_out), .out(out_3[3]), .sel(bit_extender_1_out[4]));
  Multiplexer #(.enable("false")) multiplexer_158 (
    .in0(multiplexer_126_out), .in1(multiplexer_110_out), .out(out_3[2]), .sel(bit_extender_1_out[4]));
  Multiplexer #(.enable("false")) multiplexer_159 (
    .in0(multiplexer_127_out), .in1(multiplexer_111_out), .out(out_3[1]), .sel(bit_extender_1_out[4]));
  Multiplexer #(.enable("false")) multiplexer_160 (
    .in0(multiplexer_128_out), .in1(multiplexer_112_out), .out(out_3[0]), .sel(bit_extender_1_out[4]));
endmodule

module L_32_bit_SLL (
  input  [31:0] B,
  input  [31:0] A,
  output [31:0] out_3
);

  wire multiplexer_1_out, multiplexer_2_out, multiplexer_3_out, multiplexer_4_out, multiplexer_5_out,
       multiplexer_6_out, multiplexer_7_out, multiplexer_8_out, multiplexer_9_out, multiplexer_10_out,
       multiplexer_11_out, multiplexer_12_out, multiplexer_13_out, multiplexer_14_out, multiplexer_15_out,
       multiplexer_16_out, multiplexer_17_out, multiplexer_18_out, multiplexer_19_out, multiplexer_20_out,
       multiplexer_21_out, multiplexer_22_out, multiplexer_23_out, multiplexer_24_out, multiplexer_25_out,
       multiplexer_26_out, multiplexer_27_out, multiplexer_28_out, multiplexer_29_out, multiplexer_30_out,
       multiplexer_31_out, multiplexer_32_out, multiplexer_33_out, multiplexer_34_out, multiplexer_35_out,
       multiplexer_36_out, multiplexer_37_out, multiplexer_38_out, multiplexer_39_out, multiplexer_40_out,
       multiplexer_41_out, multiplexer_42_out, multiplexer_43_out, multiplexer_44_out, multiplexer_45_out,
       multiplexer_46_out, multiplexer_47_out, multiplexer_48_out, multiplexer_49_out, multiplexer_50_out,
       multiplexer_51_out, multiplexer_52_out, multiplexer_53_out, multiplexer_54_out, multiplexer_55_out,
       multiplexer_56_out, multiplexer_57_out, multiplexer_58_out, multiplexer_59_out, multiplexer_60_out,
       multiplexer_61_out, multiplexer_62_out, multiplexer_63_out, multiplexer_64_out, multiplexer_65_out,
       multiplexer_66_out, multiplexer_67_out, multiplexer_68_out, multiplexer_69_out, multiplexer_70_out,
       multiplexer_71_out, multiplexer_72_out, multiplexer_73_out, multiplexer_74_out, multiplexer_75_out,
       multiplexer_76_out, multiplexer_77_out, multiplexer_78_out, multiplexer_79_out, multiplexer_80_out,
       multiplexer_81_out, multiplexer_82_out, multiplexer_83_out, multiplexer_84_out, multiplexer_85_out,
       multiplexer_86_out, multiplexer_87_out, multiplexer_88_out, multiplexer_89_out, multiplexer_90_out,
       multiplexer_91_out, multiplexer_92_out, multiplexer_93_out, multiplexer_94_out, multiplexer_95_out,
       multiplexer_96_out, multiplexer_97_out, multiplexer_98_out, multiplexer_99_out, multiplexer_100_out,
       multiplexer_101_out, multiplexer_102_out, multiplexer_103_out, multiplexer_104_out,
       multiplexer_105_out, multiplexer_106_out, multiplexer_107_out, multiplexer_108_out,
       multiplexer_109_out, multiplexer_110_out, multiplexer_111_out, multiplexer_112_out,
       multiplexer_113_out, multiplexer_114_out, multiplexer_115_out, multiplexer_116_out,
       multiplexer_117_out, multiplexer_118_out, multiplexer_119_out, multiplexer_120_out,
       multiplexer_121_out, multiplexer_122_out, multiplexer_123_out, multiplexer_124_out,
       multiplexer_125_out, multiplexer_126_out, multiplexer_127_out, multiplexer_128_out;
  wire [4:0] bit_extender_1_out;

  Bit_Extender #(.in_width(32), .out_width(5)) bit_extender_1 (.in(B), .out(bit_extender_1_out));
  Multiplexer #(.enable("false")) multiplexer_1 (
    .in0(A[0]), .in1(1'b0), .out(multiplexer_1_out), .sel(bit_extender_1_out[0]));
  Multiplexer #(.enable("false")) multiplexer_2 (
    .in0(A[1]), .in1(A[0]), .out(multiplexer_2_out), .sel(bit_extender_1_out[0]));
  Multiplexer #(.enable("false")) multiplexer_3 (
    .in0(A[2]), .in1(A[1]), .out(multiplexer_3_out), .sel(bit_extender_1_out[0]));
  Multiplexer #(.enable("false")) multiplexer_4 (
    .in0(A[3]), .in1(A[2]), .out(multiplexer_4_out), .sel(bit_extender_1_out[0]));
  Multiplexer #(.enable("false")) multiplexer_5 (
    .in0(A[4]), .in1(A[3]), .out(multiplexer_5_out), .sel(bit_extender_1_out[0]));
  Multiplexer #(.enable("false")) multiplexer_6 (
    .in0(A[5]), .in1(A[4]), .out(multiplexer_6_out), .sel(bit_extender_1_out[0]));
  Multiplexer #(.enable("false")) multiplexer_7 (
    .in0(A[6]), .in1(A[5]), .out(multiplexer_7_out), .sel(bit_extender_1_out[0]));
  Multiplexer #(.enable("false")) multiplexer_8 (
    .in0(A[7]), .in1(A[6]), .out(multiplexer_8_out), .sel(bit_extender_1_out[0]));
  Multiplexer #(.enable("false")) multiplexer_9 (
    .in0(A[8]), .in1(A[7]), .out(multiplexer_9_out), .sel(bit_extender_1_out[0]));
  Multiplexer #(.enable("false")) multiplexer_10 (
    .in0(A[9]), .in1(A[8]), .out(multiplexer_10_out), .sel(bit_extender_1_out[0]));
  Multiplexer #(.enable("false")) multiplexer_11 (
    .in0(A[10]), .in1(A[9]), .out(multiplexer_11_out), .sel(bit_extender_1_out[0]));
  Multiplexer #(.enable("false")) multiplexer_12 (
    .in0(A[11]), .in1(A[10]), .out(multiplexer_12_out), .sel(bit_extender_1_out[0]));
  Multiplexer #(.enable("false")) multiplexer_13 (
    .in0(A[12]), .in1(A[11]), .out(multiplexer_13_out), .sel(bit_extender_1_out[0]));
  Multiplexer #(.enable("false")) multiplexer_14 (
    .in0(A[13]), .in1(A[12]), .out(multiplexer_14_out), .sel(bit_extender_1_out[0]));
  Multiplexer #(.enable("false")) multiplexer_15 (
    .in0(A[14]), .in1(A[13]), .out(multiplexer_15_out), .sel(bit_extender_1_out[0]));
  Multiplexer #(.enable("false")) multiplexer_16 (
    .in0(A[15]), .in1(A[14]), .out(multiplexer_16_out), .sel(bit_extender_1_out[0]));
  Multiplexer #(.enable("false")) multiplexer_17 (
    .in0(A[16]), .in1(A[15]), .out(multiplexer_17_out), .sel(bit_extender_1_out[0]));
  Multiplexer #(.enable("false")) multiplexer_18 (
    .in0(A[17]), .in1(A[16]), .out(multiplexer_18_out), .sel(bit_extender_1_out[0]));
  Multiplexer #(.enable("false")) multiplexer_19 (
    .in0(A[18]), .in1(A[17]), .out(multiplexer_19_out), .sel(bit_extender_1_out[0]));
  Multiplexer #(.enable("false")) multiplexer_20 (
    .in0(A[19]), .in1(A[18]), .out(multiplexer_20_out), .sel(bit_extender_1_out[0]));
  Multiplexer #(.enable("false")) multiplexer_21 (
    .in0(A[20]), .in1(A[19]), .out(multiplexer_21_out), .sel(bit_extender_1_out[0]));
  Multiplexer #(.enable("false")) multiplexer_22 (
    .in0(A[21]), .in1(A[20]), .out(multiplexer_22_out), .sel(bit_extender_1_out[0]));
  Multiplexer #(.enable("false")) multiplexer_23 (
    .in0(A[22]), .in1(A[21]), .out(multiplexer_23_out), .sel(bit_extender_1_out[0]));
  Multiplexer #(.enable("false")) multiplexer_24 (
    .in0(A[23]), .in1(A[22]), .out(multiplexer_24_out), .sel(bit_extender_1_out[0]));
  Multiplexer #(.enable("false")) multiplexer_25 (
    .in0(A[24]), .in1(A[23]), .out(multiplexer_25_out), .sel(bit_extender_1_out[0]));
  Multiplexer #(.enable("false")) multiplexer_26 (
    .in0(A[25]), .in1(A[24]), .out(multiplexer_26_out), .sel(bit_extender_1_out[0]));
  Multiplexer #(.enable("false")) multiplexer_27 (
    .in0(A[26]), .in1(A[25]), .out(multiplexer_27_out), .sel(bit_extender_1_out[0]));
  Multiplexer #(.enable("false")) multiplexer_28 (
    .in0(A[27]), .in1(A[26]), .out(multiplexer_28_out), .sel(bit_extender_1_out[0]));
  Multiplexer #(.enable("false")) multiplexer_29 (
    .in0(A[28]), .in1(A[27]), .out(multiplexer_29_out), .sel(bit_extender_1_out[0]));
  Multiplexer #(.enable("false")) multiplexer_30 (
    .in0(A[29]), .in1(A[28]), .out(multiplexer_30_out), .sel(bit_extender_1_out[0]));
  Multiplexer #(.enable("false")) multiplexer_31 (
    .in0(A[30]), .in1(A[29]), .out(multiplexer_31_out), .sel(bit_extender_1_out[0]));
  Multiplexer #(.enable("false")) multiplexer_32 (
    .in0(A[31]), .in1(A[30]), .out(multiplexer_32_out), .sel(bit_extender_1_out[0]));
  Multiplexer #(.enable("false")) multiplexer_33 (
    .in0(multiplexer_1_out), .in1(1'b0), .out(multiplexer_33_out), .sel(bit_extender_1_out[1]));
  Multiplexer #(.enable("false")) multiplexer_34 (
    .in0(multiplexer_2_out), .in1(1'b0), .out(multiplexer_34_out), .sel(bit_extender_1_out[1]));
  Multiplexer #(.enable("false")) multiplexer_35 (
    .in0(multiplexer_3_out), .in1(multiplexer_1_out), .out(multiplexer_35_out), .sel(bit_extender_1_out[1]));
  Multiplexer #(.enable("false")) multiplexer_36 (
    .in0(multiplexer_4_out), .in1(multiplexer_2_out), .out(multiplexer_36_out), .sel(bit_extender_1_out[1]));
  Multiplexer #(.enable("false")) multiplexer_37 (
    .in0(multiplexer_5_out), .in1(multiplexer_3_out), .out(multiplexer_37_out), .sel(bit_extender_1_out[1]));
  Multiplexer #(.enable("false")) multiplexer_38 (
    .in0(multiplexer_6_out), .in1(multiplexer_4_out), .out(multiplexer_38_out), .sel(bit_extender_1_out[1]));
  Multiplexer #(.enable("false")) multiplexer_39 (
    .in0(multiplexer_7_out), .in1(multiplexer_5_out), .out(multiplexer_39_out), .sel(bit_extender_1_out[1]));
  Multiplexer #(.enable("false")) multiplexer_40 (
    .in0(multiplexer_8_out), .in1(multiplexer_6_out), .out(multiplexer_40_out), .sel(bit_extender_1_out[1]));
  Multiplexer #(.enable("false")) multiplexer_41 (
    .in0(multiplexer_9_out), .in1(multiplexer_7_out), .out(multiplexer_41_out), .sel(bit_extender_1_out[1]));
  Multiplexer #(.enable("false")) multiplexer_42 (
    .in0(multiplexer_10_out), .in1(multiplexer_8_out), .out(multiplexer_42_out), .sel(bit_extender_1_out[1]));
  Multiplexer #(.enable("false")) multiplexer_43 (
    .in0(multiplexer_11_out), .in1(multiplexer_9_out), .out(multiplexer_43_out), .sel(bit_extender_1_out[1]));
  Multiplexer #(.enable("false")) multiplexer_44 (
    .in0(multiplexer_12_out), .in1(multiplexer_10_out), .out(multiplexer_44_out), .sel(bit_extender_1_out[1]));
  Multiplexer #(.enable("false")) multiplexer_45 (
    .in0(multiplexer_13_out), .in1(multiplexer_11_out), .out(multiplexer_45_out), .sel(bit_extender_1_out[1]));
  Multiplexer #(.enable("false")) multiplexer_46 (
    .in0(multiplexer_14_out), .in1(multiplexer_12_out), .out(multiplexer_46_out), .sel(bit_extender_1_out[1]));
  Multiplexer #(.enable("false")) multiplexer_47 (
    .in0(multiplexer_15_out), .in1(multiplexer_13_out), .out(multiplexer_47_out), .sel(bit_extender_1_out[1]));
  Multiplexer #(.enable("false")) multiplexer_48 (
    .in0(multiplexer_16_out), .in1(multiplexer_14_out), .out(multiplexer_48_out), .sel(bit_extender_1_out[1]));
  Multiplexer #(.enable("false")) multiplexer_49 (
    .in0(multiplexer_17_out), .in1(multiplexer_15_out), .out(multiplexer_49_out), .sel(bit_extender_1_out[1]));
  Multiplexer #(.enable("false")) multiplexer_50 (
    .in0(multiplexer_18_out), .in1(multiplexer_16_out), .out(multiplexer_50_out), .sel(bit_extender_1_out[1]));
  Multiplexer #(.enable("false")) multiplexer_51 (
    .in0(multiplexer_19_out), .in1(multiplexer_17_out), .out(multiplexer_51_out), .sel(bit_extender_1_out[1]));
  Multiplexer #(.enable("false")) multiplexer_52 (
    .in0(multiplexer_20_out), .in1(multiplexer_18_out), .out(multiplexer_52_out), .sel(bit_extender_1_out[1]));
  Multiplexer #(.enable("false")) multiplexer_53 (
    .in0(multiplexer_21_out), .in1(multiplexer_19_out), .out(multiplexer_53_out), .sel(bit_extender_1_out[1]));
  Multiplexer #(.enable("false")) multiplexer_54 (
    .in0(multiplexer_22_out), .in1(multiplexer_20_out), .out(multiplexer_54_out), .sel(bit_extender_1_out[1]));
  Multiplexer #(.enable("false")) multiplexer_55 (
    .in0(multiplexer_23_out), .in1(multiplexer_21_out), .out(multiplexer_55_out), .sel(bit_extender_1_out[1]));
  Multiplexer #(.enable("false")) multiplexer_56 (
    .in0(multiplexer_24_out), .in1(multiplexer_22_out), .out(multiplexer_56_out), .sel(bit_extender_1_out[1]));
  Multiplexer #(.enable("false")) multiplexer_57 (
    .in0(multiplexer_25_out), .in1(multiplexer_23_out), .out(multiplexer_57_out), .sel(bit_extender_1_out[1]));
  Multiplexer #(.enable("false")) multiplexer_58 (
    .in0(multiplexer_26_out), .in1(multiplexer_24_out), .out(multiplexer_58_out), .sel(bit_extender_1_out[1]));
  Multiplexer #(.enable("false")) multiplexer_59 (
    .in0(multiplexer_27_out), .in1(multiplexer_25_out), .out(multiplexer_59_out), .sel(bit_extender_1_out[1]));
  Multiplexer #(.enable("false")) multiplexer_60 (
    .in0(multiplexer_28_out), .in1(multiplexer_26_out), .out(multiplexer_60_out), .sel(bit_extender_1_out[1]));
  Multiplexer #(.enable("false")) multiplexer_61 (
    .in0(multiplexer_29_out), .in1(multiplexer_27_out), .out(multiplexer_61_out), .sel(bit_extender_1_out[1]));
  Multiplexer #(.enable("false")) multiplexer_62 (
    .in0(multiplexer_30_out), .in1(multiplexer_28_out), .out(multiplexer_62_out), .sel(bit_extender_1_out[1]));
  Multiplexer #(.enable("false")) multiplexer_63 (
    .in0(multiplexer_31_out), .in1(multiplexer_29_out), .out(multiplexer_63_out), .sel(bit_extender_1_out[1]));
  Multiplexer #(.enable("false")) multiplexer_64 (
    .in0(multiplexer_32_out), .in1(multiplexer_30_out), .out(multiplexer_64_out), .sel(bit_extender_1_out[1]));
  Multiplexer #(.enable("false")) multiplexer_65 (
    .in0(multiplexer_33_out), .in1(1'b0), .out(multiplexer_65_out), .sel(bit_extender_1_out[2]));
  Multiplexer #(.enable("false")) multiplexer_66 (
    .in0(multiplexer_34_out), .in1(1'b0), .out(multiplexer_66_out), .sel(bit_extender_1_out[2]));
  Multiplexer #(.enable("false")) multiplexer_67 (
    .in0(multiplexer_35_out), .in1(1'b0), .out(multiplexer_67_out), .sel(bit_extender_1_out[2]));
  Multiplexer #(.enable("false")) multiplexer_68 (
    .in0(multiplexer_36_out), .in1(1'b0), .out(multiplexer_68_out), .sel(bit_extender_1_out[2]));
  Multiplexer #(.enable("false")) multiplexer_69 (
    .in0(multiplexer_37_out), .in1(multiplexer_33_out), .out(multiplexer_69_out), .sel(bit_extender_1_out[2]));
  Multiplexer #(.enable("false")) multiplexer_70 (
    .in0(multiplexer_38_out), .in1(multiplexer_34_out), .out(multiplexer_70_out), .sel(bit_extender_1_out[2]));
  Multiplexer #(.enable("false")) multiplexer_71 (
    .in0(multiplexer_39_out), .in1(multiplexer_35_out), .out(multiplexer_71_out), .sel(bit_extender_1_out[2]));
  Multiplexer #(.enable("false")) multiplexer_72 (
    .in0(multiplexer_40_out), .in1(multiplexer_36_out), .out(multiplexer_72_out), .sel(bit_extender_1_out[2]));
  Multiplexer #(.enable("false")) multiplexer_73 (
    .in0(multiplexer_41_out), .in1(multiplexer_37_out), .out(multiplexer_73_out), .sel(bit_extender_1_out[2]));
  Multiplexer #(.enable("false")) multiplexer_74 (
    .in0(multiplexer_42_out), .in1(multiplexer_38_out), .out(multiplexer_74_out), .sel(bit_extender_1_out[2]));
  Multiplexer #(.enable("false")) multiplexer_75 (
    .in0(multiplexer_43_out), .in1(multiplexer_39_out), .out(multiplexer_75_out), .sel(bit_extender_1_out[2]));
  Multiplexer #(.enable("false")) multiplexer_76 (
    .in0(multiplexer_44_out), .in1(multiplexer_40_out), .out(multiplexer_76_out), .sel(bit_extender_1_out[2]));
  Multiplexer #(.enable("false")) multiplexer_77 (
    .in0(multiplexer_45_out), .in1(multiplexer_41_out), .out(multiplexer_77_out), .sel(bit_extender_1_out[2]));
  Multiplexer #(.enable("false")) multiplexer_78 (
    .in0(multiplexer_46_out), .in1(multiplexer_42_out), .out(multiplexer_78_out), .sel(bit_extender_1_out[2]));
  Multiplexer #(.enable("false")) multiplexer_79 (
    .in0(multiplexer_47_out), .in1(multiplexer_43_out), .out(multiplexer_79_out), .sel(bit_extender_1_out[2]));
  Multiplexer #(.enable("false")) multiplexer_80 (
    .in0(multiplexer_48_out), .in1(multiplexer_44_out), .out(multiplexer_80_out), .sel(bit_extender_1_out[2]));
  Multiplexer #(.enable("false")) multiplexer_81 (
    .in0(multiplexer_49_out), .in1(multiplexer_45_out), .out(multiplexer_81_out), .sel(bit_extender_1_out[2]));
  Multiplexer #(.enable("false")) multiplexer_82 (
    .in0(multiplexer_50_out), .in1(multiplexer_46_out), .out(multiplexer_82_out), .sel(bit_extender_1_out[2]));
  Multiplexer #(.enable("false")) multiplexer_83 (
    .in0(multiplexer_51_out), .in1(multiplexer_47_out), .out(multiplexer_83_out), .sel(bit_extender_1_out[2]));
  Multiplexer #(.enable("false")) multiplexer_84 (
    .in0(multiplexer_52_out), .in1(multiplexer_48_out), .out(multiplexer_84_out), .sel(bit_extender_1_out[2]));
  Multiplexer #(.enable("false")) multiplexer_85 (
    .in0(multiplexer_53_out), .in1(multiplexer_49_out), .out(multiplexer_85_out), .sel(bit_extender_1_out[2]));
  Multiplexer #(.enable("false")) multiplexer_86 (
    .in0(multiplexer_54_out), .in1(multiplexer_50_out), .out(multiplexer_86_out), .sel(bit_extender_1_out[2]));
  Multiplexer #(.enable("false")) multiplexer_87 (
    .in0(multiplexer_55_out), .in1(multiplexer_51_out), .out(multiplexer_87_out), .sel(bit_extender_1_out[2]));
  Multiplexer #(.enable("false")) multiplexer_88 (
    .in0(multiplexer_56_out), .in1(multiplexer_52_out), .out(multiplexer_88_out), .sel(bit_extender_1_out[2]));
  Multiplexer #(.enable("false")) multiplexer_89 (
    .in0(multiplexer_57_out), .in1(multiplexer_53_out), .out(multiplexer_89_out), .sel(bit_extender_1_out[2]));
  Multiplexer #(.enable("false")) multiplexer_90 (
    .in0(multiplexer_58_out), .in1(multiplexer_54_out), .out(multiplexer_90_out), .sel(bit_extender_1_out[2]));
  Multiplexer #(.enable("false")) multiplexer_91 (
    .in0(multiplexer_59_out), .in1(multiplexer_55_out), .out(multiplexer_91_out), .sel(bit_extender_1_out[2]));
  Multiplexer #(.enable("false")) multiplexer_92 (
    .in0(multiplexer_60_out), .in1(multiplexer_56_out), .out(multiplexer_92_out), .sel(bit_extender_1_out[2]));
  Multiplexer #(.enable("false")) multiplexer_93 (
    .in0(multiplexer_61_out), .in1(multiplexer_57_out), .out(multiplexer_93_out), .sel(bit_extender_1_out[2]));
  Multiplexer #(.enable("false")) multiplexer_94 (
    .in0(multiplexer_62_out), .in1(multiplexer_58_out), .out(multiplexer_94_out), .sel(bit_extender_1_out[2]));
  Multiplexer #(.enable("false")) multiplexer_95 (
    .in0(multiplexer_63_out), .in1(multiplexer_59_out), .out(multiplexer_95_out), .sel(bit_extender_1_out[2]));
  Multiplexer #(.enable("false")) multiplexer_96 (
    .in0(multiplexer_64_out), .in1(multiplexer_60_out), .out(multiplexer_96_out), .sel(bit_extender_1_out[2]));
  Multiplexer #(.enable("false")) multiplexer_97 (
    .in0(multiplexer_65_out), .in1(1'b0), .out(multiplexer_97_out), .sel(bit_extender_1_out[3]));
  Multiplexer #(.enable("false")) multiplexer_98 (
    .in0(multiplexer_66_out), .in1(1'b0), .out(multiplexer_98_out), .sel(bit_extender_1_out[3]));
  Multiplexer #(.enable("false")) multiplexer_99 (
    .in0(multiplexer_67_out), .in1(1'b0), .out(multiplexer_99_out), .sel(bit_extender_1_out[3]));
  Multiplexer #(.enable("false")) multiplexer_100 (
    .in0(multiplexer_68_out), .in1(1'b0), .out(multiplexer_100_out), .sel(bit_extender_1_out[3]));
  Multiplexer #(.enable("false")) multiplexer_101 (
    .in0(multiplexer_69_out), .in1(1'b0), .out(multiplexer_101_out), .sel(bit_extender_1_out[3]));
  Multiplexer #(.enable("false")) multiplexer_102 (
    .in0(multiplexer_70_out), .in1(1'b0), .out(multiplexer_102_out), .sel(bit_extender_1_out[3]));
  Multiplexer #(.enable("false")) multiplexer_103 (
    .in0(multiplexer_71_out), .in1(1'b0), .out(multiplexer_103_out), .sel(bit_extender_1_out[3]));
  Multiplexer #(.enable("false")) multiplexer_104 (
    .in0(multiplexer_72_out), .in1(1'b0), .out(multiplexer_104_out), .sel(bit_extender_1_out[3]));
  Multiplexer #(.enable("false")) multiplexer_105 (
    .in0(multiplexer_73_out), .in1(multiplexer_65_out), .out(multiplexer_105_out), .sel(bit_extender_1_out[3]));
  Multiplexer #(.enable("false")) multiplexer_106 (
    .in0(multiplexer_74_out), .in1(multiplexer_66_out), .out(multiplexer_106_out), .sel(bit_extender_1_out[3]));
  Multiplexer #(.enable("false")) multiplexer_107 (
    .in0(multiplexer_75_out), .in1(multiplexer_67_out), .out(multiplexer_107_out), .sel(bit_extender_1_out[3]));
  Multiplexer #(.enable("false")) multiplexer_108 (
    .in0(multiplexer_76_out), .in1(multiplexer_68_out), .out(multiplexer_108_out), .sel(bit_extender_1_out[3]));
  Multiplexer #(.enable("false")) multiplexer_109 (
    .in0(multiplexer_77_out), .in1(multiplexer_69_out), .out(multiplexer_109_out), .sel(bit_extender_1_out[3]));
  Multiplexer #(.enable("false")) multiplexer_110 (
    .in0(multiplexer_78_out), .in1(multiplexer_70_out), .out(multiplexer_110_out), .sel(bit_extender_1_out[3]));
  Multiplexer #(.enable("false")) multiplexer_111 (
    .in0(multiplexer_79_out), .in1(multiplexer_71_out), .out(multiplexer_111_out), .sel(bit_extender_1_out[3]));
  Multiplexer #(.enable("false")) multiplexer_112 (
    .in0(multiplexer_80_out), .in1(multiplexer_72_out), .out(multiplexer_112_out), .sel(bit_extender_1_out[3]));
  Multiplexer #(.enable("false")) multiplexer_113 (
    .in0(multiplexer_81_out), .in1(multiplexer_73_out), .out(multiplexer_113_out), .sel(bit_extender_1_out[3]));
  Multiplexer #(.enable("false")) multiplexer_114 (
    .in0(multiplexer_82_out), .in1(multiplexer_74_out), .out(multiplexer_114_out), .sel(bit_extender_1_out[3]));
  Multiplexer #(.enable("false")) multiplexer_115 (
    .in0(multiplexer_83_out), .in1(multiplexer_75_out), .out(multiplexer_115_out), .sel(bit_extender_1_out[3]));
  Multiplexer #(.enable("false")) multiplexer_116 (
    .in0(multiplexer_84_out), .in1(multiplexer_76_out), .out(multiplexer_116_out), .sel(bit_extender_1_out[3]));
  Multiplexer #(.enable("false")) multiplexer_117 (
    .in0(multiplexer_85_out), .in1(multiplexer_77_out), .out(multiplexer_117_out), .sel(bit_extender_1_out[3]));
  Multiplexer #(.enable("false")) multiplexer_118 (
    .in0(multiplexer_86_out), .in1(multiplexer_78_out), .out(multiplexer_118_out), .sel(bit_extender_1_out[3]));
  Multiplexer #(.enable("false")) multiplexer_119 (
    .in0(multiplexer_87_out), .in1(multiplexer_79_out), .out(multiplexer_119_out), .sel(bit_extender_1_out[3]));
  Multiplexer #(.enable("false")) multiplexer_120 (
    .in0(multiplexer_88_out), .in1(multiplexer_80_out), .out(multiplexer_120_out), .sel(bit_extender_1_out[3]));
  Multiplexer #(.enable("false")) multiplexer_121 (
    .in0(multiplexer_89_out), .in1(multiplexer_81_out), .out(multiplexer_121_out), .sel(bit_extender_1_out[3]));
  Multiplexer #(.enable("false")) multiplexer_122 (
    .in0(multiplexer_90_out), .in1(multiplexer_82_out), .out(multiplexer_122_out), .sel(bit_extender_1_out[3]));
  Multiplexer #(.enable("false")) multiplexer_123 (
    .in0(multiplexer_91_out), .in1(multiplexer_83_out), .out(multiplexer_123_out), .sel(bit_extender_1_out[3]));
  Multiplexer #(.enable("false")) multiplexer_124 (
    .in0(multiplexer_92_out), .in1(multiplexer_84_out), .out(multiplexer_124_out), .sel(bit_extender_1_out[3]));
  Multiplexer #(.enable("false")) multiplexer_125 (
    .in0(multiplexer_93_out), .in1(multiplexer_85_out), .out(multiplexer_125_out), .sel(bit_extender_1_out[3]));
  Multiplexer #(.enable("false")) multiplexer_126 (
    .in0(multiplexer_94_out), .in1(multiplexer_86_out), .out(multiplexer_126_out), .sel(bit_extender_1_out[3]));
  Multiplexer #(.enable("false")) multiplexer_127 (
    .in0(multiplexer_95_out), .in1(multiplexer_87_out), .out(multiplexer_127_out), .sel(bit_extender_1_out[3]));
  Multiplexer #(.enable("false")) multiplexer_128 (
    .in0(multiplexer_96_out), .in1(multiplexer_88_out), .out(multiplexer_128_out), .sel(bit_extender_1_out[3]));
  Multiplexer #(.enable("false")) multiplexer_129 (
    .in0(multiplexer_97_out), .in1(1'b0), .out(out_3[0]), .sel(bit_extender_1_out[4]));
  Multiplexer #(.enable("false")) multiplexer_130 (
    .in0(multiplexer_98_out), .in1(1'b0), .out(out_3[1]), .sel(bit_extender_1_out[4]));
  Multiplexer #(.enable("false")) multiplexer_131 (
    .in0(multiplexer_99_out), .in1(1'b0), .out(out_3[2]), .sel(bit_extender_1_out[4]));
  Multiplexer #(.enable("false")) multiplexer_132 (
    .in0(multiplexer_100_out), .in1(1'b0), .out(out_3[3]), .sel(bit_extender_1_out[4]));
  Multiplexer #(.enable("false")) multiplexer_133 (
    .in0(multiplexer_101_out), .in1(1'b0), .out(out_3[4]), .sel(bit_extender_1_out[4]));
  Multiplexer #(.enable("false")) multiplexer_134 (
    .in0(multiplexer_102_out), .in1(1'b0), .out(out_3[5]), .sel(bit_extender_1_out[4]));
  Multiplexer #(.enable("false")) multiplexer_135 (
    .in0(multiplexer_103_out), .in1(1'b0), .out(out_3[6]), .sel(bit_extender_1_out[4]));
  Multiplexer #(.enable("false")) multiplexer_136 (
    .in0(multiplexer_104_out), .in1(1'b0), .out(out_3[7]), .sel(bit_extender_1_out[4]));
  Multiplexer #(.enable("false")) multiplexer_137 (
    .in0(multiplexer_105_out), .in1(1'b0), .out(out_3[8]), .sel(bit_extender_1_out[4]));
  Multiplexer #(.enable("false")) multiplexer_138 (
    .in0(multiplexer_106_out), .in1(1'b0), .out(out_3[9]), .sel(bit_extender_1_out[4]));
  Multiplexer #(.enable("false")) multiplexer_139 (
    .in0(multiplexer_107_out), .in1(1'b0), .out(out_3[10]), .sel(bit_extender_1_out[4]));
  Multiplexer #(.enable("false")) multiplexer_140 (
    .in0(multiplexer_108_out), .in1(1'b0), .out(out_3[11]), .sel(bit_extender_1_out[4]));
  Multiplexer #(.enable("false")) multiplexer_141 (
    .in0(multiplexer_109_out), .in1(1'b0), .out(out_3[12]), .sel(bit_extender_1_out[4]));
  Multiplexer #(.enable("false")) multiplexer_142 (
    .in0(multiplexer_110_out), .in1(1'b0), .out(out_3[13]), .sel(bit_extender_1_out[4]));
  Multiplexer #(.enable("false")) multiplexer_143 (
    .in0(multiplexer_111_out), .in1(1'b0), .out(out_3[14]), .sel(bit_extender_1_out[4]));
  Multiplexer #(.enable("false")) multiplexer_144 (
    .in0(multiplexer_112_out), .in1(1'b0), .out(out_3[15]), .sel(bit_extender_1_out[4]));
  Multiplexer #(.enable("false")) multiplexer_145 (
    .in0(multiplexer_113_out), .in1(multiplexer_97_out), .out(out_3[16]), .sel(bit_extender_1_out[4]));
  Multiplexer #(.enable("false")) multiplexer_146 (
    .in0(multiplexer_114_out), .in1(multiplexer_98_out), .out(out_3[17]), .sel(bit_extender_1_out[4]));
  Multiplexer #(.enable("false")) multiplexer_147 (
    .in0(multiplexer_115_out), .in1(multiplexer_99_out), .out(out_3[18]), .sel(bit_extender_1_out[4]));
  Multiplexer #(.enable("false")) multiplexer_148 (
    .in0(multiplexer_116_out), .in1(multiplexer_100_out), .out(out_3[19]), .sel(bit_extender_1_out[4]));
  Multiplexer #(.enable("false")) multiplexer_149 (
    .in0(multiplexer_117_out), .in1(multiplexer_101_out), .out(out_3[20]), .sel(bit_extender_1_out[4]));
  Multiplexer #(.enable("false")) multiplexer_150 (
    .in0(multiplexer_118_out), .in1(multiplexer_102_out), .out(out_3[21]), .sel(bit_extender_1_out[4]));
  Multiplexer #(.enable("false")) multiplexer_151 (
    .in0(multiplexer_119_out), .in1(multiplexer_103_out), .out(out_3[22]), .sel(bit_extender_1_out[4]));
  Multiplexer #(.enable("false")) multiplexer_152 (
    .in0(multiplexer_120_out), .in1(multiplexer_104_out), .out(out_3[23]), .sel(bit_extender_1_out[4]));
  Multiplexer #(.enable("false")) multiplexer_153 (
    .in0(multiplexer_121_out), .in1(multiplexer_105_out), .out(out_3[24]), .sel(bit_extender_1_out[4]));
  Multiplexer #(.enable("false")) multiplexer_154 (
    .in0(multiplexer_122_out), .in1(multiplexer_106_out), .out(out_3[25]), .sel(bit_extender_1_out[4]));
  Multiplexer #(.enable("false")) multiplexer_155 (
    .in0(multiplexer_123_out), .in1(multiplexer_107_out), .out(out_3[26]), .sel(bit_extender_1_out[4]));
  Multiplexer #(.enable("false")) multiplexer_156 (
    .in0(multiplexer_124_out), .in1(multiplexer_108_out), .out(out_3[27]), .sel(bit_extender_1_out[4]));
  Multiplexer #(.enable("false")) multiplexer_157 (
    .in0(multiplexer_125_out), .in1(multiplexer_109_out), .out(out_3[28]), .sel(bit_extender_1_out[4]));
  Multiplexer #(.enable("false")) multiplexer_158 (
    .in0(multiplexer_126_out), .in1(multiplexer_110_out), .out(out_3[29]), .sel(bit_extender_1_out[4]));
  Multiplexer #(.enable("false")) multiplexer_159 (
    .in0(multiplexer_127_out), .in1(multiplexer_111_out), .out(out_3[30]), .sel(bit_extender_1_out[4]));
  Multiplexer #(.enable("false")) multiplexer_160 (
    .in0(multiplexer_128_out), .in1(multiplexer_112_out), .out(out_3[31]), .sel(bit_extender_1_out[4]));
endmodule

module sllx (
  input  [31:0] in_1,
  input  [31:0] in_2,
  output [31:0] out_3
);

  Shifter #(.width(32)) shifter_1 (.in(in_1), .\dist (in_2[4:0]), .out(out_3));
endmodule

module srlx (
  input  [31:0] in_1,
  input  [31:0] in_2,
  output [31:0] out_3
);

  Shifter #(.shift("lr"), .width(32)) shifter_1 (.in(in_1), .\dist (in_2[4:0]), .out(out_3));
endmodule

module mult (
  input  [31:0] b0a,
  input  cin,
  input  [31:0] astatic,
  input  bn,
  output outputR,
  output cout,
  output [31:0] nuevoA,
  output [31:0] astatico
);

  wire [31:0] and_1_out, bit_extender_1_out;

  assign bit_extender_1_out = {{31{bn}}, bn};  // Bit_Extender bit_extender_1
  assign and_1_out = astatic & bit_extender_1_out;  // AND_Gate and_1, 32 bits wide
  L_32_bit_Adder l_32_bit_adder_1 (.A({cin, b0a[31:1]}), .B(and_1_out), .overflow(cout), .Result(nuevoA));

  assign astatico = astatic;
  assign outputR = nuevoA[0];
endmodule

module mult32 (
  input  [31:0] A,
  input  [31:0] B,
  output [31:0] mflo,
  output [31:0] mfhi,
  output overflow
);

  wire mult_1_cout, mult_2_cout, mult_3_cout, mult_4_cout, mult_5_cout, mult_6_cout, mult_7_cout,
       mult_8_cout, mult_9_cout, mult_10_cout, mult_11_cout, mult_12_cout, mult_13_cout, mult_14_cout,
       mult_15_cout, mult_16_cout, mult_17_cout, mult_18_cout, mult_19_cout, mult_20_cout, mult_21_cout,
       mult_22_cout, mult_23_cout, mult_24_cout, mult_25_cout, mult_26_cout, mult_27_cout, mult_28_cout,
       mult_29_cout, mult_30_cout;
  wire [1:0] and_1_out;
  wire [31:0] bit_extender_1_out, mult_1_astatico, mult_1_nuevoa, mult_2_astatico, mult_2_nuevoa,
       mult_3_astatico, mult_3_nuevoa, mult_4_astatico, mult_4_nuevoa, mult_5_astatico, mult_5_nuevoa,
       mult_6_astatico, mult_6_nuevoa, mult_7_astatico, mult_7_nuevoa, mult_8_astatico, mult_8_nuevoa,
       mult_9_astatico, mult_9_nuevoa, mult_10_astatico, mult_10_nuevoa, mult_11_astatico, mult_11_nuevoa,
       mult_12_astatico, mult_12_nuevoa, mult_13_astatico, mult_13_nuevoa, mult_14_astatico, mult_14_nuevoa,
       mult_15_astatico, mult_15_nuevoa, mult_16_astatico, mult_16_nuevoa, mult_17_astatico, mult_17_nuevoa,
       mult_18_astatico, mult_18_nuevoa, mult_19_astatico, mult_19_nuevoa, mult_20_astatico, mult_20_nuevoa,
       mult_21_astatico, mult_21_nuevoa, mult_22_astatico, mult_22_nuevoa, mult_23_astatico, mult_23_nuevoa,
       mult_24_astatico, mult_24_nuevoa, mult_25_astatico, mult_25_nuevoa, mult_26_astatico, mult_26_nuevoa,
       mult_27_astatico, mult_27_nuevoa, mult_28_astatico, mult_28_nuevoa, mult_29_astatico, mult_29_nuevoa,
       mult_30_astatico, mult_30_nuevoa;
  wire [31:3] and_1_out_2;

  assign bit_extender_1_out = {{31{B[0]}}, B[0]};  // Bit_Extender bit_extender_1
  assign {and_1_out_2, and_1_out, mflo[0]} = A & bit_extender_1_out;  // AND_Gate and_1, 32 bits wide
  mult mult_1 (
    .b0a({and_1_out_2, and_1_out, mflo[0]}), .cin(1'b0), .astatic(A), .bn(B[1]), .outputR(mflo[1]),
    .cout(mult_1_cout), .nuevoA(mult_1_nuevoa), .astatico(mult_1_astatico));
  mult mult_2 (
    .b0a(mult_1_nuevoa), .cin(mult_1_cout), .astatic(mult_1_astatico), .bn(B[2]), .outputR(mflo[2]),
    .cout(mult_2_cout), .nuevoA(mult_2_nuevoa), .astatico(mult_2_astatico));
  mult mult_3 (
    .b0a(mult_2_nuevoa), .cin(mult_2_cout), .astatic(mult_2_astatico), .bn(B[3]), .outputR(mflo[3]),
    .cout(mult_3_cout), .nuevoA(mult_3_nuevoa), .astatico(mult_3_astatico));
  mult mult_4 (
    .b0a(mult_3_nuevoa), .cin(mult_3_cout), .astatic(mult_3_astatico), .bn(B[4]), .outputR(mflo[4]),
    .cout(mult_4_cout), .nuevoA(mult_4_nuevoa), .astatico(mult_4_astatico));
  mult mult_5 (
    .b0a(mult_4_nuevoa), .cin(mult_4_cout), .astatic(mult_4_astatico), .bn(B[5]), .outputR(mflo[5]),
    .cout(mult_5_cout), .nuevoA(mult_5_nuevoa), .astatico(mult_5_astatico));
  mult mult_6 (
    .b0a(mult_5_nuevoa), .cin(mult_5_cout), .astatic(mult_5_astatico), .bn(B[6]), .outputR(mflo[6]),
    .cout(mult_6_cout), .nuevoA(mult_6_nuevoa), .astatico(mult_6_astatico));
  mult mult_7 (
    .b0a(mult_6_nuevoa), .cin(mult_6_cout), .astatic(mult_6_astatico), .bn(B[7]), .outputR(mflo[7]),
    .cout(mult_7_cout), .nuevoA(mult_7_nuevoa), .astatico(mult_7_astatico));
  mult mult_8 (
    .b0a(mult_7_nuevoa), .cin(mult_7_cout), .astatic(mult_7_astatico), .bn(B[8]), .outputR(mflo[8]),
    .cout(mult_8_cout), .nuevoA(mult_8_nuevoa), .astatico(mult_8_astatico));
  mult mult_9 (
    .b0a(mult_8_nuevoa), .cin(mult_8_cout), .astatic(mult_8_astatico), .bn(B[9]), .outputR(mflo[9]),
    .cout(mult_9_cout), .nuevoA(mult_9_nuevoa), .astatico(mult_9_astatico));
  mult mult_10 (
    .b0a(mult_9_nuevoa), .cin(mult_9_cout), .astatic(mult_9_astatico), .bn(B[10]), .outputR(mflo[10]),
    .cout(mult_10_cout), .nuevoA(mult_10_nuevoa), .astatico(mult_10_astatico));
  mult mult_11 (
    .b0a(mult_10_nuevoa), .cin(mult_10_cout), .astatic(mult_10_astatico), .bn(B[11]), .outputR(mflo[11]),
    .cout(mult_11_cout), .nuevoA(mult_11_nuevoa), .astatico(mult_11_astatico));
  mult mult_12 (
    .b0a(mult_11_nuevoa), .cin(mult_11_cout), .astatic(mult_11_astatico), .bn(B[12]), .outputR(mflo[12]),
    .cout(mult_12_cout), .nuevoA(mult_12_nuevoa), .astatico(mult_12_astatico));
  mult mult_13 (
    .b0a(mult_12_nuevoa), .cin(mult_12_cout), .astatic(mult_12_astatico), .bn(B[13]), .outputR(mflo[13]),
    .cout(mult_13_cout), .nuevoA(mult_13_nuevoa), .astatico(mult_13_astatico));
  mult mult_14 (
    .b0a(mult_13_nuevoa), .cin(mult_13_cout), .astatic(mult_13_astatico), .bn(B[14]), .outputR(mflo[14]),
    .cout(mult_14_cout), .nuevoA(mult_14_nuevoa), .astatico(mult_14_astatico));
  mult mult_15 (
    .b0a(mult_14_nuevoa), .cin(mult_14_cout), .astatic(mult_14_astatico), .bn(B[15]), .outputR(mflo[15]),
    .cout(mult_15_cout), .nuevoA(mult_15_nuevoa), .astatico(mult_15_astatico));
  mult mult_16 (
    .b0a(mult_15_nuevoa), .cin(mult_15_cout), .astatic(mult_15_astatico), .bn(B[16]), .outputR(mflo[16]),
    .cout(mult_16_cout), .nuevoA(mult_16_nuevoa), .astatico(mult_16_astatico));
  mult mult_17 (
    .b0a(mult_16_nuevoa), .cin(mult_16_cout), .astatic(mult_16_astatico), .bn(B[17]), .outputR(mflo[17]),
    .cout(mult_17_cout), .nuevoA(mult_17_nuevoa), .astatico(mult_17_astatico));
  mult mult_18 (
    .b0a(mult_17_nuevoa), .cin(mult_17_cout), .astatic(mult_17_astatico), .bn(B[18]), .outputR(mflo[18]),
    .cout(mult_18_cout), .nuevoA(mult_18_nuevoa), .astatico(mult_18_astatico));
  mult mult_19 (
    .b0a(mult_18_nuevoa), .cin(mult_18_cout), .astatic(mult_18_astatico), .bn(B[19]), .outputR(mflo[19]),
    .cout(mult_19_cout), .nuevoA(mult_19_nuevoa), .astatico(mult_19_astatico));
  mult mult_20 (
    .b0a(mult_19_nuevoa), .cin(mult_19_cout), .astatic(mult_19_astatico), .bn(B[20]), .outputR(mflo[20]),
    .cout(mult_20_cout), .nuevoA(mult_20_nuevoa), .astatico(mult_20_astatico));
  mult mult_21 (
    .b0a(mult_20_nuevoa), .cin(mult_20_cout), .astatic(mult_20_astatico), .bn(B[21]), .outputR(mflo[21]),
    .cout(mult_21_cout), .nuevoA(mult_21_nuevoa), .astatico(mult_21_astatico));
  mult mult_22 (
    .b0a(mult_21_nuevoa), .cin(mult_21_cout), .astatic(mult_21_astatico), .bn(B[22]), .outputR(mflo[22]),
    .cout(mult_22_cout), .nuevoA(mult_22_nuevoa), .astatico(mult_22_astatico));
  mult mult_23 (
    .b0a(mult_22_nuevoa), .cin(mult_22_cout), .astatic(mult_22_astatico), .bn(B[23]), .outputR(mflo[23]),
    .cout(mult_23_cout), .nuevoA(mult_23_nuevoa), .astatico(mult_23_astatico));
  mult mult_24 (
    .b0a(mult_23_nuevoa), .cin(mult_23_cout), .astatic(mult_23_astatico), .bn(B[24]), .outputR(mflo[24]),
    .cout(mult_24_cout), .nuevoA(mult_24_nuevoa), .astatico(mult_24_astatico));
  mult mult_25 (
    .b0a(mult_24_nuevoa), .cin(mult_24_cout), .astatic(mult_24_astatico), .bn(B[25]), .outputR(mflo[25]),
    .cout(mult_25_cout), .nuevoA(mult_25_nuevoa), .astatico(mult_25_astatico));
  mult mult_26 (
    .b0a(mult_25_nuevoa), .cin(mult_25_cout), .astatic(mult_25_astatico), .bn(B[26]), .outputR(mflo[26]),
    .cout(mult_26_cout), .nuevoA(mult_26_nuevoa), .astatico(mult_26_astatico));
  mult mult_27 (
    .b0a(mult_26_nuevoa), .cin(mult_26_cout), .astatic(mult_26_astatico), .bn(B[27]), .outputR(mflo[27]),
    .cout(mult_27_cout), .nuevoA(mult_27_nuevoa), .astatico(mult_27_astatico));
  mult mult_28 (
    .b0a(mult_27_nuevoa), .cin(mult_27_cout), .astatic(mult_27_astatico), .bn(B[28]), .outputR(mflo[28]),
    .cout(mult_28_cout), .nuevoA(mult_28_nuevoa), .astatico(mult_28_astatico));
  mult mult_29 (
    .b0a(mult_28_nuevoa), .cin(mult_28_cout), .astatic(mult_28_astatico), .bn(B[29]), .outputR(mflo[29]),
    .cout(mult_29_cout), .nuevoA(mult_29_nuevoa), .astatico(mult_29_astatico));
  mult mult_30 (
    .b0a(mult_29_nuevoa), .cin(mult_29_cout), .astatic(mult_29_astatico), .bn(B[30]), .outputR(mflo[30]),
    .cout(mult_30_cout), .nuevoA(mult_30_nuevoa), .astatico(mult_30_astatico));
  mult mult_31 (
    .b0a(mult_30_nuevoa), .cin(mult_30_cout), .astatic(mult_30_astatico), .bn(B[31]), .outputR(mflo[31]),
    .cout(overflow), .nuevoA(mfhi));  // open: astatico
endmodule

module L_1_bit_register (
  input  D,
  input  CLK,
  output Q,
  output Q_neg
);

  wire nand_1_out, nand_2_out, nand_3_out, nand_4_out, nand_5_out, nand_6_out, not_1_out;

  nand nand_1 (nand_1_out, D, CLK);
  nand nand_2 (nand_2_out, nand_1_out, CLK);
  not not_1 (not_1_out, CLK);
  nand nand_3 (nand_3_out, nand_1_out, nand_4_out);
  nand nand_4 (nand_4_out, nand_3_out, nand_2_out);
  nand nand_5 (nand_5_out, nand_3_out, not_1_out);
  nand nand_6 (nand_6_out, not_1_out, nand_4_out);
  nand nand_7 (Q, nand_5_out, Q_neg);
  nand nand_8 (Q_neg, Q, nand_6_out);
endmodule

module L_32_bit_register (
  input  CLK,
  input  [31:0] DATA,
  output [31:0] Q,
  output [31:0] Q_neg
);

  wire nand_1_out, nand_2_out, nand_3_out, nand_4_out, nand_5_out, nand_6_out, nand_7_out, nand_8_out,
       nand_9_out, nand_10_out, nand_11_out, nand_12_out, nand_13_out, nand_14_out, nand_15_out, nand_16_out,
       nand_17_out, nand_18_out, nand_19_out, nand_20_out, nand_21_out, nand_22_out, nand_23_out,
       nand_24_out, nand_25_out, nand_26_out, nand_27_out, nand_28_out, nand_29_out, nand_30_out,
       nand_31_out, nand_32_out, nand_33_out, nand_34_out, nand_35_out, nand_36_out, nand_37_out,
       nand_38_out, nand_39_out, nand_40_out, nand_41_out, nand_42_out, nand_43_out, nand_44_out,
       nand_45_out, nand_46_out, nand_47_out, nand_48_out, nand_49_out, nand_50_out, nand_51_out,
       nand_52_out, nand_53_out, nand_54_out, nand_55_out, nand_56_out, nand_57_out, nand_58_out,
       nand_59_out, nand_60_out, nand_61_out, nand_62_out, nand_63_out, nand_64_out, nand_65_out,
       nand_66_out, nand_67_out, nand_68_out, nand_69_out, nand_70_out, nand_71_out, nand_72_out,
       nand_73_out, nand_74_out, nand_75_out, nand_76_out, nand_77_out, nand_78_out, nand_79_out,
       nand_80_out, nand_81_out, nand_82_out, nand_83_out, nand_84_out, nand_85_out, nand_86_out,
       nand_87_out, nand_88_out, nand_89_out, nand_90_out, nand_91_out, nand_92_out, nand_93_out,
       nand_94_out, nand_95_out, nand_96_out, nand_129_out, nand_130_out, nand_131_out, nand_132_out,
       nand_133_out, nand_134_out, nand_135_out, nand_136_out, nand_137_out, nand_138_out, nand_139_out,
       nand_140_out, nand_141_out, nand_142_out, nand_143_out, nand_144_out, nand_145_out, nand_146_out,
       nand_147_out, nand_148_out, nand_149_out, nand_150_out, nand_151_out, nand_152_out, nand_153_out,
       nand_154_out, nand_155_out, nand_156_out, nand_157_out, nand_158_out, nand_159_out, nand_160_out,
       nand_161_out, nand_162_out, nand_163_out, nand_164_out, nand_165_out, nand_166_out, nand_167_out,
       nand_168_out, nand_169_out, nand_170_out, nand_171_out, nand_172_out, nand_173_out, nand_174_out,
       nand_175_out, nand_176_out, nand_177_out, nand_178_out, nand_179_out, nand_180_out, nand_181_out,
       nand_182_out, nand_183_out, nand_184_out, nand_185_out, nand_186_out, nand_187_out, nand_188_out,
       nand_189_out, nand_190_out, nand_191_out, nand_192_out, nand_193_out, nand_194_out, nand_195_out,
       nand_196_out, nand_197_out, nand_198_out, nand_199_out, nand_200_out, nand_201_out, nand_202_out,
       nand_203_out, nand_204_out, nand_205_out, nand_206_out, nand_207_out, nand_208_out, nand_209_out,
       nand_210_out, nand_211_out, nand_212_out, nand_213_out, nand_214_out, nand_215_out, nand_216_out,
       nand_217_out, nand_218_out, nand_219_out, nand_220_out, nand_221_out, nand_222_out, nand_223_out,
       nand_224_out, not_1_out, not_2_out, not_3_out, not_4_out, not_5_out, not_6_out, not_7_out, not_8_out,
       not_9_out, not_10_out, not_11_out, not_12_out, not_13_out, not_14_out, not_15_out, not_16_out,
       not_17_out, not_18_out, not_19_out, not_20_out, not_21_out, not_22_out, not_23_out, not_24_out,
       not_25_out, not_26_out, not_27_out, not_28_out, not_29_out, not_30_out, not_31_out, not_32_out;

  nand nand_1 (nand_1_out, DATA[16], CLK);
  nand nand_2 (nand_2_out, nand_1_out, CLK);
  nand nand_3 (nand_3_out, DATA[17], CLK);
  nand nand_4 (nand_4_out, nand_3_out, CLK);
  nand nand_5 (nand_5_out, DATA[18], CLK);
  nand nand_6 (nand_6_out, nand_5_out, CLK);
  nand nand_7 (nand_7_out, DATA[19], CLK);
  nand nand_8 (nand_8_out, nand_7_out, CLK);
  nand nand_9 (nand_9_out, DATA[20], CLK);
  nand nand_10 (nand_10_out, nand_9_out, CLK);
  nand nand_11 (nand_11_out, DATA[21], CLK);
  nand nand_12 (nand_12_out, nand_11_out, CLK);
  nand nand_13 (nand_13_out, DATA[22], CLK);
  nand nand_14 (nand_14_out, nand_13_out, CLK);
  nand nand_15 (nand_15_out, DATA[23], CLK);
  nand nand_16 (nand_16_out, nand_15_out, CLK);
  nand nand_17 (nand_17_out, DATA[24], CLK);
  nand nand_18 (nand_18_out, nand_17_out, CLK);
  nand nand_19 (nand_19_out, DATA[25], CLK);
  nand nand_20 (nand_20_out, nand_19_out, CLK);
  nand nand_21 (nand_21_out, DATA[26], CLK);
  nand nand_22 (nand_22_out, nand_21_out, CLK);
  nand nand_23 (nand_23_out, DATA[27], CLK);
  nand nand_24 (nand_24_out, nand_23_out, CLK);
  nand nand_25 (nand_25_out, DATA[28], CLK);
  nand nand_26 (nand_26_out, nand_25_out, CLK);
  nand nand_27 (nand_27_out, DATA[29], CLK);
  nand nand_28 (nand_28_out, nand_27_out, CLK);
  nand nand_29 (nand_29_out, DATA[30], CLK);
  nand nand_30 (nand_30_out, nand_29_out, CLK);
  not not_1 (not_1_out, CLK);
  not not_2 (not_2_out, CLK);
  not not_3 (not_3_out, CLK);
  not not_4 (not_4_out, CLK);
  not not_5 (not_5_out, CLK);
  not not_6 (not_6_out, CLK);
  not not_7 (not_7_out, CLK);
  not not_8 (not_8_out, CLK);
  not not_9 (not_9_out, CLK);
  not not_10 (not_10_out, CLK);
  not not_11 (not_11_out, CLK);
  not not_12 (not_12_out, CLK);
  not not_13 (not_13_out, CLK);
  not not_14 (not_14_out, CLK);
  not not_15 (not_15_out, CLK);
  nand nand_31 (nand_31_out, DATA[31], CLK);
  nand nand_32 (nand_32_out, nand_31_out, CLK);
  not not_16 (not_16_out, CLK);
  nand nand_33 (nand_33_out, nand_1_out, nand_34_out);
  nand nand_34 (nand_34_out, nand_33_out, nand_2_out);
  nand nand_35 (nand_35_out, nand_3_out, nand_36_out);
  nand nand_36 (nand_36_out, nand_35_out, nand_4_out);
  nand nand_37 (nand_37_out, nand_5_out, nand_38_out);
  nand nand_38 (nand_38_out, nand_37_out, nand_6_out);
  nand nand_39 (nand_39_out, nand_7_out, nand_40_out);
  nand nand_40 (nand_40_out, nand_39_out, nand_8_out);
  nand nand_41 (nand_41_out, nand_9_out, nand_42_out);
  nand nand_42 (nand_42_out, nand_41_out, nand_10_out);
  nand nand_43 (nand_43_out, nand_11_out, nand_44_out);
  nand nand_44 (nand_44_out, nand_43_out, nand_12_out);
  nand nand_45 (nand_45_out, nand_13_out, nand_46_out);
  nand nand_46 (nand_46_out, nand_45_out, nand_14_out);
  nand nand_47 (nand_47_out, nand_15_out, nand_48_out);
  nand nand_48 (nand_48_out, nand_47_out, nand_16_out);
  nand nand_49 (nand_49_out, nand_17_out, nand_50_out);
  nand nand_50 (nand_50_out, nand_49_out, nand_18_out);
  nand nand_51 (nand_51_out, nand_19_out, nand_52_out);
  nand nand_52 (nand_52_out, nand_51_out, nand_20_out);
  nand nand_53 (nand_53_out, nand_21_out, nand_54_out);
  nand nand_54 (nand_54_out, nand_53_out, nand_22_out);
  nand nand_55 (nand_55_out, nand_23_out, nand_56_out);
  nand nand_56 (nand_56_out, nand_55_out, nand_24_out);
  nand nand_57 (nand_57_out, nand_25_out, nand_58_out);
  nand nand_58 (nand_58_out, nand_57_out, nand_26_out);
  nand nand_59 (nand_59_out, nand_27_out, nand_60_out);
  nand nand_60 (nand_60_out, nand_59_out, nand_28_out);
  nand nand_61 (nand_61_out, nand_29_out, nand_62_out);
  nand nand_62 (nand_62_out, nand_61_out, nand_30_out);
  nand nand_63 (nand_63_out, nand_31_out, nand_64_out);
  nand nand_64 (nand_64_out, nand_63_out, nand_32_out);
  nand nand_65 (nand_65_out, nand_33_out, not_1_out);
  nand nand_66 (nand_66_out, not_1_out, nand_34_out);
  nand nand_67 (nand_67_out, nand_35_out, not_2_out);
  nand nand_68 (nand_68_out, not_2_out, nand_36_out);
  nand nand_69 (nand_69_out, nand_37_out, not_3_out);
  nand nand_70 (nand_70_out, not_3_out, nand_38_out);
  nand nand_71 (nand_71_out, nand_39_out, not_4_out);
  nand nand_72 (nand_72_out, not_4_out, nand_40_out);
  nand nand_73 (nand_73_out, nand_41_out, not_5_out);
  nand nand_74 (nand_74_out, not_5_out, nand_42_out);
  nand nand_75 (nand_75_out, nand_43_out, not_6_out);
  nand nand_76 (nand_76_out, not_6_out, nand_44_out);
  nand nand_77 (nand_77_out, nand_45_out, not_7_out);
  nand nand_78 (nand_78_out, not_7_out, nand_46_out);
  nand nand_79 (nand_79_out, nand_47_out, not_8_out);
  nand nand_80 (nand_80_out, not_8_out, nand_48_out);
  nand nand_81 (nand_81_out, nand_49_out, not_9_out);
  nand nand_82 (nand_82_out, not_9_out, nand_50_out);
  nand nand_83 (nand_83_out, nand_51_out, not_10_out);
  nand nand_84 (nand_84_out, not_10_out, nand_52_out);
  nand nand_85 (nand_85_out, nand_53_out, not_11_out);
  nand nand_86 (nand_86_out, not_11_out, nand_54_out);
  nand nand_87 (nand_87_out, nand_55_out, not_12_out);
  nand nand_88 (nand_88_out, not_12_out, nand_56_out);
  nand nand_89 (nand_89_out, nand_57_out, not_13_out);
  nand nand_90 (nand_90_out, not_13_out, nand_58_out);
  nand nand_91 (nand_91_out, nand_59_out, not_14_out);
  nand nand_92 (nand_92_out, not_14_out, nand_60_out);
  nand nand_93 (nand_93_out, nand_61_out, not_15_out);
  nand nand_94 (nand_94_out, not_15_out, nand_62_out);
  nand nand_95 (nand_95_out, nand_63_out, not_16_out);
  nand nand_96 (nand_96_out, not_16_out, nand_64_out);
  nand nand_97 (Q[16], nand_65_out, Q_neg[16]);
  nand nand_98 (Q_neg[16], Q[16], nand_66_out);
  nand nand_99 (Q[18], nand_69_out, Q_neg[18]);
  nand nand_100 (Q_neg[18], Q[18], nand_70_out);
  nand nand_101 (Q[17], nand_67_out, Q_neg[17]);
  nand nand_102 (Q_neg[17], Q[17], nand_68_out);
  nand nand_103 (Q[19], nand_71_out, Q_neg[19]);
  nand nand_104 (Q_neg[19], Q[19], nand_72_out);
  nand nand_105 (Q[20], nand_73_out, Q_neg[20]);
  nand nand_106 (Q_neg[20], Q[20], nand_74_out);
  nand nand_107 (Q[21], nand_75_out, Q_neg[21]);
  nand nand_108 (Q_neg[21], Q[21], nand_76_out);
  nand nand_109 (Q[22], nand_77_out, Q_neg[22]);
  nand nand_110 (Q_neg[22], Q[22], nand_78_out);
  nand nand_111 (Q[23], nand_79_out, Q_neg[23]);
  nand nand_112 (Q_neg[23], Q[23], nand_80_out);
  nand nand_113 (Q[24], nand_81_out, Q_neg[24]);
  nand nand_114 (Q_neg[24], Q[24], nand_82_out);
  nand nand_115 (Q[25], nand_83_out, Q_neg[25]);
  nand nand_116 (Q_neg[25], Q[25], nand_84_out);
  nand nand_117 (Q[26], nand_85_out, Q_neg[26]);
  nand nand_118 (Q_neg[26], Q[26], nand_86_out);
  nand nand_119 (Q[27], nand_87_out, Q_neg[27]);
  nand nand_120 (Q_neg[27], Q[27], nand_88_out);
  nand nand_121 (Q[28], nand_89_out, Q_neg[28]);
  nand nand_122 (Q_neg[28], Q[28], nand_90_out);
  nand nand_123 (Q[29], nand_91_out, Q_neg[29]);
  nand nand_124 (Q_neg[29], Q[29], nand_92_out);
  nand nand_125 (Q[30], nand_93_out, Q_neg[30]);
  nand nand_126 (Q_neg[30], Q[30], nand_94_out);
  nand nand_127 (Q[31], nand_95_out, Q_neg[31]);
  nand nand_128 (Q_neg[31], Q[31], nand_96_out);
  nand nand_129 (nand_129_out, DATA[0], CLK);
  nand nand_130 (nand_130_out, nand_129_out, CLK);
  not not_17 (not_17_out, CLK);
  nand nand_131 (nand_131_out, DATA[1], CLK);
  nand nand_132 (nand_132_out, nand_131_out, CLK);
  nand nand_133 (nand_133_out, DATA[2], CLK);
  nand nand_134 (nand_134_out, nand_133_out, CLK);
  not not_18 (not_18_out, CLK);
  nand nand_135 (nand_135_out, DATA[3], CLK);
  nand nand_136 (nand_136_out, nand_135_out, CLK);
  nand nand_137 (nand_137_out, DATA[4], CLK);
  nand nand_138 (nand_138_out, nand_137_out, CLK);
  nand nand_139 (nand_139_out, DATA[5], CLK);
  nand nand_140 (nand_140_out, nand_139_out, CLK);
  nand nand_141 (nand_141_out, DATA[6], CLK);
  nand nand_142 (nand_142_out, nand_141_out, CLK);
  nand nand_143 (nand_143_out, DATA[7], CLK);
  nand nand_144 (nand_144_out, nand_143_out, CLK);
  nand nand_145 (nand_145_out, DATA[8], CLK);
  nand nand_146 (nand_146_out, nand_145_out, CLK);
  nand nand_147 (nand_147_out, DATA[9], CLK);
  nand nand_148 (nand_148_out, nand_147_out, CLK);
  nand nand_149 (nand_149_out, DATA[10], CLK);
  nand nand_150 (nand_150_out, nand_149_out, CLK);
  nand nand_151 (nand_151_out, DATA[11], CLK);
  nand nand_152 (nand_152_out, nand_151_out, CLK);
  nand nand_153 (nand_153_out, DATA[12], CLK);
  nand nand_154 (nand_154_out, nand_153_out, CLK);
  nand nand_155 (nand_155_out, DATA[13], CLK);
  nand nand_156 (nand_156_out, nand_155_out, CLK);
  nand nand_157 (nand_157_out, DATA[14], CLK);
  nand nand_158 (nand_158_out, nand_157_out, CLK);
  nand nand_159 (nand_159_out, DATA[15], CLK);
  nand nand_160 (nand_160_out, nand_159_out, CLK);
  not not_19 (not_19_out, CLK);
  not not_20 (not_20_out, CLK);
  not not_21 (not_21_out, CLK);
  not not_22 (not_22_out, CLK);
  not not_23 (not_23_out, CLK);
  not not_24 (not_24_out, CLK);
  not not_25 (not_25_out, CLK);
  not not_26 (not_26_out, CLK);
  not not_27 (not_27_out, CLK);
  not not_28 (not_28_out, CLK);
  not not_29 (not_29_out, CLK);
  not not_30 (not_30_out, CLK);
  not not_31 (not_31_out, CLK);
  not not_32 (not_32_out, CLK);
  nand nand_161 (nand_161_out, nand_129_out, nand_162_out);
  nand nand_162 (nand_162_out, nand_161_out, nand_130_out);
  nand nand_163 (nand_163_out, nand_131_out, nand_164_out);
  nand nand_164 (nand_164_out, nand_163_out, nand_132_out);
  nand nand_165 (nand_165_out, nand_133_out, nand_166_out);
  nand nand_166 (nand_166_out, nand_165_out, nand_134_out);
  nand nand_167 (nand_167_out, nand_135_out, nand_168_out);
  nand nand_168 (nand_168_out, nand_167_out, nand_136_out);
  nand nand_169 (nand_169_out, nand_137_out, nand_170_out);
  nand nand_170 (nand_170_out, nand_169_out, nand_138_out);
  nand nand_171 (nand_171_out, nand_139_out, nand_172_out);
  nand nand_172 (nand_172_out, nand_171_out, nand_140_out);
  nand nand_173 (nand_173_out, nand_141_out, nand_174_out);
  nand nand_174 (nand_174_out, nand_173_out, nand_142_out);
  nand nand_175 (nand_175_out, nand_143_out, nand_176_out);
  nand nand_176 (nand_176_out, nand_175_out, nand_144_out);
  nand nand_177 (nand_177_out, nand_145_out, nand_178_out);
  nand nand_178 (nand_178_out, nand_177_out, nand_146_out);
  nand nand_179 (nand_179_out, nand_147_out, nand_180_out);
  nand nand_180 (nand_180_out, nand_179_out, nand_148_out);
  nand nand_181 (nand_181_out, nand_149_out, nand_182_out);
  nand nand_182 (nand_182_out, nand_181_out, nand_150_out);
  nand nand_183 (nand_183_out, nand_151_out, nand_184_out);
  nand nand_184 (nand_184_out, nand_183_out, nand_152_out);
  nand nand_185 (nand_185_out, nand_153_out, nand_186_out);
  nand nand_186 (nand_186_out, nand_185_out, nand_154_out);
  nand nand_187 (nand_187_out, nand_155_out, nand_188_out);
  nand nand_188 (nand_188_out, nand_187_out, nand_156_out);
  nand nand_189 (nand_189_out, nand_157_out, nand_190_out);
  nand nand_190 (nand_190_out, nand_189_out, nand_158_out);
  nand nand_191 (nand_191_out, nand_159_out, nand_192_out);
  nand nand_192 (nand_192_out, nand_191_out, nand_160_out);
  nand nand_193 (nand_193_out, nand_161_out, not_17_out);
  nand nand_194 (nand_194_out, nand_165_out, not_18_out);
  nand nand_195 (nand_195_out, not_17_out, nand_162_out);
  nand nand_196 (nand_196_out, nand_163_out, not_19_out);
  nand nand_197 (nand_197_out, not_19_out, nand_164_out);
  nand nand_198 (nand_198_out, not_18_out, nand_166_out);
  nand nand_199 (nand_199_out, nand_167_out, not_20_out);
  nand nand_200 (nand_200_out, not_20_out, nand_168_out);
  nand nand_201 (nand_201_out, nand_169_out, not_21_out);
  nand nand_202 (nand_202_out, not_21_out, nand_170_out);
  nand nand_203 (nand_203_out, nand_171_out, not_22_out);
  nand nand_204 (nand_204_out, not_22_out, nand_172_out);
  nand nand_205 (nand_205_out, nand_173_out, not_23_out);
  nand nand_206 (nand_206_out, not_23_out, nand_174_out);
  nand nand_207 (nand_207_out, nand_175_out, not_24_out);
  nand nand_208 (nand_208_out, not_24_out, nand_176_out);
  nand nand_209 (nand_209_out, nand_177_out, not_25_out);
  nand nand_210 (nand_210_out, not_25_out, nand_178_out);
  nand nand_211 (nand_211_out, nand_179_out, not_26_out);
  nand nand_212 (nand_212_out, not_26_out, nand_180_out);
  nand nand_213 (nand_213_out, nand_181_out, not_27_out);
  nand nand_214 (nand_214_out, not_27_out, nand_182_out);
  nand nand_215 (nand_215_out, nand_183_out, not_28_out);
  nand nand_216 (nand_216_out, not_28_out, nand_184_out);
  nand nand_217 (nand_217_out, nand_185_out, not_29_out);
  nand nand_218 (nand_218_out, not_29_out, nand_186_out);
  nand nand_219 (nand_219_out, nand_187_out, not_30_out);
  nand nand_220 (nand_220_out, not_30_out, nand_188_out);
  nand nand_221 (nand_221_out, nand_189_out, not_31_out);
  nand nand_222 (nand_222_out, not_31_out, nand_190_out);
  nand nand_223 (nand_223_out, nand_191_out, not_32_out);
  nand nand_224 (nand_224_out, not_32_out, nand_192_out);
  nand nand_225 (Q[0], nand_193_out, Q_neg[0]);
  nand nand_226 (Q_neg[0], Q[0], nand_195_out);
  nand nand_227 (Q[1], nand_196_out, Q_neg[1]);
  nand nand_228 (Q_neg[1], Q[1], nand_197_out);
  nand nand_229 (Q[2], nand_194_out, Q_neg[2]);
  nand nand_230 (Q_neg[2], Q[2], nand_198_out);
  nand nand_231 (Q[3], nand_199_out, Q_neg[3]);
  nand nand_232 (Q_neg[3], Q[3], nand_200_out);
  nand nand_233 (Q[4], nand_201_out, Q_neg[4]);
  nand nand_234 (Q_neg[4], Q[4], nand_202_out);
  nand nand_235 (Q[5], nand_203_out, Q_neg[5]);
  nand nand_236 (Q_neg[5], Q[5], nand_204_out);
  nand nand_237 (Q[6], nand_205_out, Q_neg[6]);
  nand nand_238 (Q_neg[6], Q[6], nand_206_out);
  nand nand_239 (Q[7], nand_207_out, Q_neg[7]);
  nand nand_240 (Q_neg[7], Q[7], nand_208_out);
  nand nand_241 (Q[8], nand_209_out, Q_neg[8]);
  nand nand_242 (Q_neg[8], Q[8], nand_210_out);
  nand nand_243 (Q[10], nand_213_out, Q_neg[10]);
  nand nand_244 (Q_neg[10], Q[10], nand_214_out);
  nand nand_245 (Q[9], nand_211_out, Q_neg[9]);
  nand nand_246 (Q_neg[9], Q[9], nand_212_out);
  nand nand_247 (Q[11], nand_215_out, Q_neg[11]);
  nand nand_248 (Q_neg[11], Q[11], nand_216_out);
  nand nand_249 (Q[12], nand_217_out, Q_neg[12]);
  nand nand_250 (Q_neg[12], Q[12], nand_218_out);
  nand nand_251 (Q[13], nand_219_out, Q_neg[13]);
  nand nand_252 (Q_neg[13], Q[13], nand_220_out);
  nand nand_253 (Q[14], nand_221_out, Q_neg[14]);
  nand nand_254 (Q_neg[14], Q[14], nand_222_out);
  nand nand_255 (Q[15], nand_223_out, Q_neg[15]);
  nand nand_256 (Q_neg[15], Q[15], nand_224_out);
endmodule
module L_32x_32_bit_reg (
  input  clock,
  input  [31:0] in_2,
  input  [31:0] in_3,
  input  [31:0] in_4,
  input  [31:0] in_5,
  input  [31:0] in_6,
  input  [31:0] in_7,
  input  [31:0] in_8,
  input  [31:0] in_9,
  input  [31:0] in_10,
  input  [31:0] in_11,
  input  [31:0] in_12,
  input  [31:0] in_13,
  input  [31:0] in_14,
  input  [31:0] in_15,
  input  [31:0] in_16,
  input  [31:0] in_17,
  input  [31:0] in_18,
  input  [31:0] in_19,
  input  [31:0] in_20,
  input  [31:0] in_21,
  input  [31:0] in_22,
  input  [31:0] in_23,
  input  [31:0] in_24,
  input  [31:0] in_25,
  input  [31:0] in_26,
  input  [31:0] in_27,
  input  [31:0] in_28,
  input  [31:0] in_29,
  input  [31:0] in_30,
  input  [31:0] in_31,
  input  [31:0] in_32,
  input  [31:0] in_33,
  output [31:0] zero,
  output [31:0] at,
  output [31:0] v0,
  output [31:0] v1,
  output [31:0] a0,
  output [31:0] a1,
  output [31:0] a2,
  output [31:0] a3,
  output [31:0] t0,
  output [31:0] t1,
  output [31:0] t2,
  output [31:0] t3,
  output [31:0] t4,
  output [31:0] t5,
  output [31:0] t6,
  output [31:0] t7,
  output [31:0] t8,
  output [31:0] t9,
  output [31:0] s0,
  output [31:0] s1,
  output [31:0] s2,
  output [31:0] s3,
  output [31:0] s4,
  output [31:0] s5,
  output [31:0] s6,
  output [31:0] s7,
  output [31:0] k0,
  output [31:0] k1,
  output [31:0] gp,
  output [31:0] sp,
  output [31:0] fp,
  output [31:0] ra
);

  L_32_bit_register l_32_bit_register_1 (.CLK(clock), .DATA(in_2), .Q(zero));  // open: Q_neg
  L_32_bit_register l_32_bit_register_2 (.CLK(clock), .DATA(in_3), .Q(at));  // open: Q_neg
  L_32_bit_register l_32_bit_register_3 (.CLK(clock), .DATA(in_4), .Q(v0));  // open: Q_neg
  L_32_bit_register l_32_bit_register_4 (.CLK(clock), .DATA(in_5), .Q(v1));  // open: Q_neg
  L_32_bit_register l_32_bit_register_5 (.CLK(clock), .DATA(in_6), .Q(a0));  // open: Q_neg
  L_32_bit_register l_32_bit_register_6 (.CLK(clock), .DATA(in_7), .Q(a1));  // open: Q_neg
  L_32_bit_register l_32_bit_register_7 (.CLK(clock), .DATA(in_8), .Q(a2));  // open: Q_neg
  L_32_bit_register l_32_bit_register_8 (.CLK(clock), .DATA(in_9), .Q(a3));  // open: Q_neg
  L_32_bit_register l_32_bit_register_9 (.CLK(clock), .DATA(in_10), .Q(t0));  // open: Q_neg
  L_32_bit_register l_32_bit_register_10 (.CLK(clock), .DATA(in_11), .Q(t1));  // open: Q_neg
  L_32_bit_register l_32_bit_register_11 (.CLK(clock), .DATA(in_12), .Q(t2));  // open: Q_neg
  L_32_bit_register l_32_bit_register_12 (.CLK(clock), .DATA(in_13), .Q(t3));  // open: Q_neg
  L_32_bit_register l_32_bit_register_13 (.CLK(clock), .DATA(in_14), .Q(t4));  // open: Q_neg
  L_32_bit_register l_32_bit_register_14 (.CLK(clock), .DATA(in_15), .Q(t5));  // open: Q_neg
  L_32_bit_register l_32_bit_register_15 (.CLK(clock), .DATA(in_16), .Q(t6));  // open: Q_neg
  L_32_bit_register l_32_bit_register_16 (.CLK(clock), .DATA(in_17), .Q(t7));  // open: Q_neg
  L_32_bit_register l_32_bit_register_17 (.CLK(clock), .DATA(in_18), .Q(t8));  // open: Q_neg
  L_32_bit_register l_32_bit_register_18 (.CLK(clock), .DATA(in_19), .Q(t9));  // open: Q_neg
  L_32_bit_register l_32_bit_register_19 (.CLK(clock), .DATA(in_20), .Q(s0));  // open: Q_neg
  L_32_bit_register l_32_bit_register_20 (.CLK(clock), .DATA(in_21), .Q(s1));  // open: Q_neg
  L_32_bit_register l_32_bit_register_21 (.CLK(clock), .DATA(in_22), .Q(s2));  // open: Q_neg
  L_32_bit_register l_32_bit_register_22 (.CLK(clock), .DATA(in_23), .Q(s3));  // open: Q_neg
  L_32_bit_register l_32_bit_register_23 (.CLK(clock), .DATA(in_24), .Q(s4));  // open: Q_neg
  L_32_bit_register l_32_bit_register_24 (.CLK(clock), .DATA(in_25), .Q(s5));  // open: Q_neg
  L_32_bit_register l_32_bit_register_25 (.CLK(clock), .DATA(in_26), .Q(s6));  // open: Q_neg
  L_32_bit_register l_32_bit_register_26 (.CLK(clock), .DATA(in_27), .Q(s7));  // open: Q_neg
  L_32_bit_register l_32_bit_register_27 (.CLK(clock), .DATA(in_28), .Q(k0));  // open: Q_neg
  L_32_bit_register l_32_bit_register_28 (.CLK(clock), .DATA(in_29), .Q(k1));  // open: Q_neg
  L_32_bit_register l_32_bit_register_29 (.CLK(clock), .DATA(in_30), .Q(gp));  // open: Q_neg
  L_32_bit_register l_32_bit_register_30 (.CLK(clock), .DATA(in_31), .Q(sp));  // open: Q_neg
  L_32_bit_register l_32_bit_register_31 (.CLK(clock), .DATA(in_32), .Q(fp));  // open: Q_neg
  L_32_bit_register l_32_bit_register_32 (.CLK(clock), .DATA(in_33), .Q(ra));  // open: Q_neg
endmodule

module L_32_bit_reg (
  input  write_enable,
  input  clock,
  input  [4:0] read_selector_1,
  input  [4:0] read_selector_2,
  input  [4:0] write_selector,
  input  [31:0] write_data,
  input  [31:0] hi_in,
  input  [31:0] low_in,
  output [31:0] output_1,
  output [31:0] output_2,
  output [31:0] hi_out,
  output [31:0] low_out
);

  wire [31:0] demultiplexer_1_out0, demultiplexer_1_out1, demultiplexer_1_out2, demultiplexer_1_out3,
       demultiplexer_1_out4, demultiplexer_1_out5, demultiplexer_1_out6, demultiplexer_1_out7,
       demultiplexer_1_out8, demultiplexer_1_out9, demultiplexer_1_out10, demultiplexer_1_out11,
       demultiplexer_1_out12, demultiplexer_1_out13, demultiplexer_1_out14, demultiplexer_1_out15,
       demultiplexer_1_out16, demultiplexer_1_out17, demultiplexer_1_out18, demultiplexer_1_out19,
       demultiplexer_1_out20, demultiplexer_1_out21, demultiplexer_1_out22, demultiplexer_1_out23,
       demultiplexer_1_out24, demultiplexer_1_out25, demultiplexer_1_out26, demultiplexer_1_out27,
       demultiplexer_1_out28, demultiplexer_1_out29, demultiplexer_1_out30, demultiplexer_1_out31,
       l_32x_32_bit_reg_1_a0, l_32x_32_bit_reg_1_a1, l_32x_32_bit_reg_1_a2, l_32x_32_bit_reg_1_a3,
       l_32x_32_bit_reg_1_at, l_32x_32_bit_reg_1_fp, l_32x_32_bit_reg_1_gp, l_32x_32_bit_reg_1_k0,
       l_32x_32_bit_reg_1_k1, l_32x_32_bit_reg_1_ra, l_32x_32_bit_reg_1_s0, l_32x_32_bit_reg_1_s1,
       l_32x_32_bit_reg_1_s2, l_32x_32_bit_reg_1_s3, l_32x_32_bit_reg_1_s4, l_32x_32_bit_reg_1_s5,
       l_32x_32_bit_reg_1_s6, l_32x_32_bit_reg_1_s7, l_32x_32_bit_reg_1_sp, l_32x_32_bit_reg_1_t0,
       l_32x_32_bit_reg_1_t1, l_32x_32_bit_reg_1_t2, l_32x_32_bit_reg_1_t3, l_32x_32_bit_reg_1_t4,
       l_32x_32_bit_reg_1_t5, l_32x_32_bit_reg_1_t6, l_32x_32_bit_reg_1_t7, l_32x_32_bit_reg_1_t8,
       l_32x_32_bit_reg_1_t9, l_32x_32_bit_reg_1_v0, l_32x_32_bit_reg_1_v1, l_32x_32_bit_reg_1_zero;

  Demultiplexer #(.select(5), .width(32)) demultiplexer_1 (
    .out0(demultiplexer_1_out0), .out1(demultiplexer_1_out1), .out2(demultiplexer_1_out2),
    .out3(demultiplexer_1_out3), .out4(demultiplexer_1_out4), .out5(demultiplexer_1_out5),
    .out6(demultiplexer_1_out6), .out7(demultiplexer_1_out7), .out8(demultiplexer_1_out8),
    .out9(demultiplexer_1_out9), .out10(demultiplexer_1_out10), .out11(demultiplexer_1_out11),
    .out12(demultiplexer_1_out12), .out13(demultiplexer_1_out13), .out14(demultiplexer_1_out14),
    .out15(demultiplexer_1_out15), .out16(demultiplexer_1_out16), .out17(demultiplexer_1_out17),
    .out18(demultiplexer_1_out18), .out19(demultiplexer_1_out19), .out20(demultiplexer_1_out20),
    .out21(demultiplexer_1_out21), .out22(demultiplexer_1_out22), .out23(demultiplexer_1_out23),
    .out24(demultiplexer_1_out24), .out25(demultiplexer_1_out25), .out26(demultiplexer_1_out26),
    .out27(demultiplexer_1_out27), .out28(demultiplexer_1_out28), .out29(demultiplexer_1_out29),
    .out30(demultiplexer_1_out30), .out31(demultiplexer_1_out31), .in(write_data), .sel(write_selector),
    .en(write_enable));
  L_32_bit_register l_32_bit_register_1 (.CLK(clock), .DATA(hi_in), .Q(hi_out));  // open: Q_neg
  L_32_bit_register l_32_bit_register_2 (.CLK(clock), .DATA(low_in), .Q(low_out));  // open: Q_neg
  L_32x_32_bit_reg l_32x_32_bit_reg_1 (
    .in_2(demultiplexer_1_out0), .in_3(demultiplexer_1_out1), .in_4(demultiplexer_1_out2),
    .in_5(demultiplexer_1_out3), .in_6(demultiplexer_1_out4), .in_7(demultiplexer_1_out5),
    .in_8(demultiplexer_1_out6), .in_9(demultiplexer_1_out7), .in_10(demultiplexer_1_out8),
    .in_11(demultiplexer_1_out9), .in_12(demultiplexer_1_out10), .in_13(demultiplexer_1_out11),
    .in_14(demultiplexer_1_out12), .in_15(demultiplexer_1_out13), .in_16(demultiplexer_1_out14),
    .in_17(demultiplexer_1_out15), .in_18(demultiplexer_1_out16), .in_19(demultiplexer_1_out17),
    .in_20(demultiplexer_1_out18), .in_21(demultiplexer_1_out19), .in_22(demultiplexer_1_out20),
    .in_23(demultiplexer_1_out21), .in_24(demultiplexer_1_out22), .in_25(demultiplexer_1_out23),
    .in_26(demultiplexer_1_out24), .in_27(demultiplexer_1_out25), .in_28(demultiplexer_1_out26),
    .in_29(demultiplexer_1_out27), .in_30(demultiplexer_1_out28), .in_31(demultiplexer_1_out29),
    .in_32(demultiplexer_1_out30), .in_33(demultiplexer_1_out31), .clock(clock),
    .zero(l_32x_32_bit_reg_1_zero), .at(l_32x_32_bit_reg_1_at), .v0(l_32x_32_bit_reg_1_v0),
    .v1(l_32x_32_bit_reg_1_v1), .a0(l_32x_32_bit_reg_1_a0), .a1(l_32x_32_bit_reg_1_a1),
    .a2(l_32x_32_bit_reg_1_a2), .a3(l_32x_32_bit_reg_1_a3), .t0(l_32x_32_bit_reg_1_t0),
    .t1(l_32x_32_bit_reg_1_t1), .t2(l_32x_32_bit_reg_1_t2), .t3(l_32x_32_bit_reg_1_t3),
    .t4(l_32x_32_bit_reg_1_t4), .t5(l_32x_32_bit_reg_1_t5), .t6(l_32x_32_bit_reg_1_t6),
    .t7(l_32x_32_bit_reg_1_t7), .t8(l_32x_32_bit_reg_1_t8), .t9(l_32x_32_bit_reg_1_t9),
    .s0(l_32x_32_bit_reg_1_s0), .s1(l_32x_32_bit_reg_1_s1), .s2(l_32x_32_bit_reg_1_s2),
    .s3(l_32x_32_bit_reg_1_s3), .s4(l_32x_32_bit_reg_1_s4), .s5(l_32x_32_bit_reg_1_s5),
    .s6(l_32x_32_bit_reg_1_s6), .s7(l_32x_32_bit_reg_1_s7), .k0(l_32x_32_bit_reg_1_k0),
    .k1(l_32x_32_bit_reg_1_k1), .gp(l_32x_32_bit_reg_1_gp), .sp(l_32x_32_bit_reg_1_sp),
    .fp(l_32x_32_bit_reg_1_fp), .ra(l_32x_32_bit_reg_1_ra));
  Multiplexer #(.enable("false"), .select(5), .width(32)) multiplexer_1 (
    .in0(l_32x_32_bit_reg_1_zero), .in1(l_32x_32_bit_reg_1_at), .in2(l_32x_32_bit_reg_1_v0),
    .in3(l_32x_32_bit_reg_1_v1), .in4(l_32x_32_bit_reg_1_a0), .in5(l_32x_32_bit_reg_1_a1),
    .in6(l_32x_32_bit_reg_1_a2), .in7(l_32x_32_bit_reg_1_a3), .in8(l_32x_32_bit_reg_1_t0),
    .in9(l_32x_32_bit_reg_1_t1), .in10(l_32x_32_bit_reg_1_t2), .in11(l_32x_32_bit_reg_1_t3),
    .in12(l_32x_32_bit_reg_1_t4), .in13(l_32x_32_bit_reg_1_t5), .in14(l_32x_32_bit_reg_1_t6),
    .in15(l_32x_32_bit_reg_1_t7), .in16(l_32x_32_bit_reg_1_t8), .in17(l_32x_32_bit_reg_1_t9),
    .in18(l_32x_32_bit_reg_1_s0), .in19(l_32x_32_bit_reg_1_s1), .in20(l_32x_32_bit_reg_1_s2),
    .in21(l_32x_32_bit_reg_1_s3), .in22(l_32x_32_bit_reg_1_s4), .in23(l_32x_32_bit_reg_1_s5),
    .in24(l_32x_32_bit_reg_1_s6), .in25(l_32x_32_bit_reg_1_s7), .in26(l_32x_32_bit_reg_1_k0),
    .in27(l_32x_32_bit_reg_1_k1), .in28(l_32x_32_bit_reg_1_gp), .in29(l_32x_32_bit_reg_1_sp),
    .in30(l_32x_32_bit_reg_1_fp), .in31(l_32x_32_bit_reg_1_ra), .out(output_1));  // open: sel
  Multiplexer #(.enable("false"), .select(5), .width(32)) multiplexer_2 (
    .in0(l_32x_32_bit_reg_1_ra), .in1(l_32x_32_bit_reg_1_fp), .in2(l_32x_32_bit_reg_1_sp),
    .in3(l_32x_32_bit_reg_1_gp), .in4(l_32x_32_bit_reg_1_k1), .in5(l_32x_32_bit_reg_1_k0),
    .in6(l_32x_32_bit_reg_1_s7), .in7(l_32x_32_bit_reg_1_s6), .in8(l_32x_32_bit_reg_1_s5),
    .in9(l_32x_32_bit_reg_1_s4), .in10(l_32x_32_bit_reg_1_s3), .in11(l_32x_32_bit_reg_1_s2),
    .in12(l_32x_32_bit_reg_1_s1), .in13(l_32x_32_bit_reg_1_s0), .in14(l_32x_32_bit_reg_1_t9),
    .in15(l_32x_32_bit_reg_1_t8), .in16(l_32x_32_bit_reg_1_t7), .in17(l_32x_32_bit_reg_1_t6),
    .in18(l_32x_32_bit_reg_1_t5), .in19(l_32x_32_bit_reg_1_t4), .in20(l_32x_32_bit_reg_1_t3),
    .in21(l_32x_32_bit_reg_1_t2), .in22(l_32x_32_bit_reg_1_t1), .in23(l_32x_32_bit_reg_1_t0),
    .in24(l_32x_32_bit_reg_1_a3), .in25(l_32x_32_bit_reg_1_a2), .in26(l_32x_32_bit_reg_1_a1),
    .in27(l_32x_32_bit_reg_1_a0), .in28(l_32x_32_bit_reg_1_v1), .in29(l_32x_32_bit_reg_1_v0),
    .in30(l_32x_32_bit_reg_1_at), .in31(l_32x_32_bit_reg_1_zero), .out(output_2));  // open: sel
endmodule
